// Logisim project ALU.circ as structural Verilog: 1 circuit, main circuit ALU
module ALU (
  input  [15:0] R,
  input  [15:0] L,
  input  [7:0] IR,
  input  [1:0] ALU_OP,
  input  USE_CARRY,
  input  MSWC,
  input  ALUOP_SZ,
  input  nDO_RSHIFT,
  output [15:0] R_SMALL_ENDIAN,
  output [15:0] L_SMALL_ENDIAN,
  output ALUV,
  output ALUC,
  output ALUS,
  output [15:0] Q,
  output ALUZ,
  output [15:0] Z_SMALL_ENDIAN,
  output [15:0] Z
);

  wire and_1_out, demultiplexer_1_out0, demultiplexer_1_out1, demultiplexer_1_out2, demultiplexer_1_out3,
       demultiplexer_1_out4, demultiplexer_1_out5, demultiplexer_1_out6, demultiplexer_1_out7, nor_1_out,
       nor_2_out, not_1_out, U1_ng, U1_np, U2_ng, U2_np, U3_ng, U3_np, U4_cn4, U4_f0, U4_f1, U4_f2, U4_f3,
       U4_ovr, U5_cn4, U5_ovr, U6_cnx, U6_cny, U6_cnz, U6_ng, U6_np, U13A_out, U14A_out, U14B_out, U15B_out,
       U17_y1, U19A_out;
  wire [2:0] U18_y2;

  // NoConnect on U6_ng
  SN74182 U6 (
    .nP3(1'b1), .nG3(1'b1), .nP2(U3_np), .nG2(U3_ng), .nP1(U1_np), .nG1(U1_ng), .nP0(U2_np), .nG0(U2_ng),
    .Cn(U14B_out), .nP(U6_np), .nG(U6_ng), .Cnz(U6_cnz), .Cny(U6_cny), .Cnx(U6_cnx));
  // NoConnect on U6_np
  SN74382 U5 (
    .Cn(U6_cnz), .A0(R[3]), .B0(L[3]), .A1(R[2]), .B1(L[2]), .A2(R[1]), .B2(L[1]), .A3(R[0]), .B3(L[0]),
    .S0(U18_y2[0]), .S1(U18_y2[1]), .S2(U18_y2[2]), .F0(Q[3]), .F1(Q[2]), .F2(Q[1]), .F3(Q[0]), .OVR(U5_ovr),
    .Cn4(U5_cn4));
  IC_74244 U9 (
    .Y3(Z[5]), .Y4(Z[4]), .Z1(Z[3]), .Y1(Z[7]), .Z2(Z[2]), .Z3(Z[1]), .Z4(Z[0]), .Y2(Z[6]), .A3(Q[4]),
    .A4(Q[3]), .OEA(nDO_RSHIFT), .B1(Q[2]), .A1(Q[6]), .B2(Q[1]), .B3(Q[0]), .B4(1'b0), .OEB(nDO_RSHIFT),
    .A2(Q[5]));
  IC_74244 U7 (
    .Y3(Z[13]), .Y4(Z[12]), .Z1(Z[11]), .Y1(Z[15]), .Z2(Z[10]), .Z3(Z[9]), .Z4(Z[8]), .Y2(Z[14]), .A3(Q[12]),
    .A4(Q[11]), .OEA(nDO_RSHIFT), .B1(Q[10]), .A1(Q[14]), .B2(Q[9]), .B3(Q[8]), .B4(Q[7]), .OEB(nDO_RSHIFT),
    .A2(Q[13]));
  SN74381 U3 (
    .Cn(U6_cny), .B0(R[7]), .A0(L[7]), .B1(R[6]), .A1(L[6]), .B2(R[5]), .A2(L[5]), .B3(R[4]), .A3(L[4]),
    .S0(U18_y2[0]), .S1(U18_y2[1]), .S2(U18_y2[2]), .F0(Q[7]), .F1(Q[6]), .F2(Q[5]), .F3(Q[4]), .nP(U3_np),
    .nG(U3_ng));
  nor nor_1 (nor_1_out, Q[0], Q[1], Q[2], Q[3], Q[4], Q[5], Q[6], Q[7]);
  nor nor_2 (nor_2_out, Q[8], Q[9], Q[10], Q[11], Q[12], Q[13], Q[14], Q[15]);
  and and_1 (and_1_out, nor_1_out, nor_2_out);
  IC_74244 U8 (
    .Y3(Z[5]), .Y4(Z[4]), .Z1(Z[3]), .Y1(Z[7]), .Z2(Z[2]), .Z3(Z[1]), .Z4(Z[0]), .Y2(Z[6]), .A3(Q[5]),
    .A4(Q[4]), .OEA(U14A_out), .B1(Q[3]), .A1(Q[7]), .B2(Q[2]), .B3(Q[1]), .B4(Q[0]), .OEB(U14A_out),
    .A2(Q[6]));
  SN74381 U1 (
    .Cn(U6_cnx), .B0(R[11]), .A0(L[11]), .B1(R[10]), .A1(L[10]), .B2(R[9]), .A2(L[9]), .B3(R[8]), .A3(L[8]),
    .S0(U18_y2[0]), .S1(U18_y2[1]), .S2(U18_y2[2]), .F0(Q[11]), .F1(Q[10]), .F2(Q[9]), .F3(Q[8]), .nP(U1_np),
    .nG(U1_ng));
  IC_74244 U10 (
    .Y3(Z[5]), .Y4(Z[4]), .Z1(Z[3]), .Y1(Z[7]), .Z2(Z[2]), .Z3(Z[1]), .Z4(Z[0]), .Y2(Z[6]), .A3(U4_f3),
    .A4(U4_f3), .OEA(U13A_out), .B1(U4_f3), .A1(U4_f3), .B2(U4_f3), .B3(U4_f3), .B4(U4_f3), .OEB(U13A_out),
    .A2(U4_f3));
  // NoConnect on U4_f2
  IC_74244 U11 (
    .Y3(Z[13]), .Y4(Z[12]), .Z1(Z[11]), .Y1(Z[15]), .Z2(Z[10]), .Z3(Z[9]), .Z4(Z[8]), .Y2(Z[14]), .A3(Q[13]),
    .A4(Q[12]), .OEA(not_1_out), .B1(Q[11]), .A1(Q[15]), .B2(Q[10]), .B3(Q[9]), .B4(Q[8]), .OEB(not_1_out),
    .A2(Q[14]));
  SN74382 U4 (
    .Cn(U6_cnx), .A0(R[11]), .B0(L[11]), .A1(R[10]), .B1(L[10]), .A2(R[9]), .B2(L[9]), .A3(R[8]), .B3(L[8]),
    .S0(U18_y2[0]), .S1(U18_y2[1]), .S2(U18_y2[2]), .F0(U4_f0), .F1(U4_f1), .F2(U4_f2), .F3(U4_f3),
    .OVR(U4_ovr), .Cn4(U4_cn4));
  // NoConnect on U4_f1
  // NoConnect on U4_f0
  REVERSE16 reverse16_1 (.MY_IN(Z), .MY_OUT(Z_SMALL_ENDIAN));
  SN74381 U2 (
    .Cn(U14B_out), .B0(R[15]), .A0(L[15]), .B1(R[14]), .A1(L[14]), .B2(R[13]), .A2(L[13]), .B3(R[12]),
    .A3(L[12]), .S0(U18_y2[0]), .S1(U18_y2[1]), .S2(U18_y2[2]), .F0(Q[15]), .F1(Q[14]), .F2(Q[13]),
    .F3(Q[12]), .nP(U2_np), .nG(U2_ng));
  Demultiplexer #(.enable("false"), .select(3)) demultiplexer_1 (
    .out0(demultiplexer_1_out0), .out1(demultiplexer_1_out1), .out2(demultiplexer_1_out2),
    .out3(demultiplexer_1_out3), .out4(demultiplexer_1_out4), .out5(demultiplexer_1_out5),
    .out6(demultiplexer_1_out6), .out7(demultiplexer_1_out7), .in(1'b1), .sel(U18_y2));
  or U14A (U14A_out, ALUOP_SZ, not_1_out);
  nand U13A (U13A_out, ALUOP_SZ, nDO_RSHIFT);
  LED CLR (.in(demultiplexer_1_out0));
  LED R_MINUS_L (.in(demultiplexer_1_out1));
  LED L_MINUS_R (.in(demultiplexer_1_out2));
  LED L_PLUS_R (.in(demultiplexer_1_out3));
  LED L_XOR_R (.in(demultiplexer_1_out4));
  LED L_OR_R (.in(demultiplexer_1_out5));
  LED L_AND_R (.in(demultiplexer_1_out6));
  LED PRESET (.in(demultiplexer_1_out7));
  or U14B (U14B_out, U15B_out, U19A_out);
  not not_1 (not_1_out, nDO_RSHIFT);
  nor U15B (U15B_out, U18_y2[0], USE_CARRY);
  and U19A (U19A_out, USE_CARRY, MSWC);
  IC_74157 U16 (
    .Y2(ALUC), .Y3(ALUS), .Y4(ALUZ), .Y1(ALUV), .A2(U5_cn4), .B2(U4_cn4), .A3(Q[0]), .B3(Q[8]),
    .A4(and_1_out), .A1(U5_ovr), .B4(nor_2_out), .S0(ALUOP_SZ), .OE(1'b0), .B1(U4_ovr));
  IC_74153 U18 (
    .Y1(U18_y2[1]), .Y2(U18_y2[0]), .C1(1'b1), .D1(1'b1), .A2(IR[3]), .A1(IR[2]), .B2(1'b0), .C2(1'b0),
    .D2(1'b1), .S0(ALU_OP[1]), .S1(ALU_OP[0]), .OE1(1'b0), .OE2(1'b0), .B1(1'b1));
  // NoConnect on U17_y1
  IC_74153 U17 (
    .Y1(U17_y1), .Y2(U18_y2[2]), .C1(1'b0), .D1(1'b0), .A2(IR[1]), .A1(1'b0), .B2(1'b1), .C2(1'b0),
    .D2(1'b0), .S0(ALU_OP[1]), .S1(ALU_OP[0]), .OE1(1'b0), .OE2(1'b0), .B1(1'b0));
  REVERSE16 reverse16_2 (.MY_IN(R), .MY_OUT(R_SMALL_ENDIAN));
  REVERSE16 reverse16_3 (.MY_IN(L), .MY_OUT(L_SMALL_ENDIAN));
endmodule
