// Logisim project CLOCKS.circ as structural Verilog: 1 circuit, main circuit CLOCKS
module CLOCKS (
  input  nHALT,
  input  [1:0] CLOCK_SELECT,
  input  MANUAL_CLK,
  input  nWAIT,
  input  nSTOP_CLK,
  input  nBP_RESET,
  output IOCLK,
  output CLKM,
  output CLKS,
  output nRESET
);

  wire and_1_out, and_2_out, and_3_out, and_4_out, d_ff_1_qn, d_ff_2_qn, d_ff_3_qn, ic_7474_1_q1,
       ic_7474_1_q2, ic_7474_1_r1, ic_7474_1_r2, multiplexer_1_out, NORMAL_CLK_out, not_1_out, not_2_out,
       or_1_out, SLOW_CLK_out, TURBO_CLK_out, U2_y, U2_z, U3_q1, U3_q2, U3_r1, U3_r2, U4A_out, U4B_out,
       U4C_out, U20A_out;

  Clock TURBO_CLK (.out(TURBO_CLK_out));
  Clock NORMAL_CLK (.out(NORMAL_CLK_out));
  Clock SLOW_CLK (.out(SLOW_CLK_out));
  not not_1 (not_1_out, nHALT);
  IC_74151 U2 (
    .Y(U2_y), .Z(U2_z), .C(SLOW_CLK_out), .D(MANUAL_CLK), .E(1'b0), .A(TURBO_CLK_out), .F(1'b0), .G(1'b0),
    .J(1'b0), .S0(CLOCK_SELECT[0]), .S1(CLOCK_SELECT[1]), .S2(not_1_out), .OE(1'b0), .B(NORMAL_CLK_out));
  and U4B (U4B_out, nSTOP_CLK, nBP_RESET);
  not U20A (U20A_out, IOCLK);
  and U4C (U4C_out, U4B_out, U20A_out);
  IC_7474 U3 (
    .R1(U3_r1), .Q2(U3_q2), .R2(U3_r2), .Q1(U3_q1), .CLK1(U2_y), .CLR1(nBP_RESET), .SET2(1'b1), .D2(nWAIT),
    .SET1(1'b1), .CLK2(U4C_out), .CLR2(nBP_RESET), .D1(U4B_out));
  // NoConnect on U3_r1
  // NoConnect on U3_q2
  // NoConnect on ic_7474_1_q1
  IC_7474 ic_7474_1 (
    .R1(ic_7474_1_r1), .Q2(ic_7474_1_q2), .R2(ic_7474_1_r2), .Q1(ic_7474_1_q1), .CLK1(U2_y), .CLR1(U3_r2),
    .SET2(1'b1), .D2(ic_7474_1_r2), .SET1(1'b1), .CLK2(ic_7474_1_r1), .CLR2(U3_r2), .D1(ic_7474_1_r1));
  and U4A (U4A_out, U2_z, U3_q1);
  buf buffer_1 (nRESET, nBP_RESET);
  Multiplexer #(.enable("false")) multiplexer_1 (
    .in0(U4A_out), .in1(ic_7474_1_q2), .out(multiplexer_1_out), .sel(U3_r2));
  not not_2 (not_2_out, nRESET);
  D_Flip_Flop d_ff_1 (
    .clk(multiplexer_1_out), .D(or_1_out), .Q(IOCLK), .Qn(d_ff_1_qn), .reset(not_2_out));  // open: preset
  D_Flip_Flop d_ff_2 (
    .clk(multiplexer_1_out), .D(and_1_out), .Q(CLKM), .Qn(d_ff_2_qn), .reset(not_2_out));  // open: preset
  and and_1 (and_1_out, IOCLK, d_ff_3_qn);
  D_Flip_Flop d_ff_3 (
    .clk(multiplexer_1_out), .D(and_2_out), .Q(CLKS), .Qn(d_ff_3_qn), .reset(not_2_out));  // open: preset
  and and_2 (and_2_out, d_ff_2_qn, d_ff_1_qn);
  // Digital_Oscilloscope #(.frontlines("falling")) digital_oscilloscope_1: pin names not known; wires that end beside it: U2_y, IOCLK, CLKM, CLKS, multiplexer_1_out, ic_7474_1_r1, ic_7474_1_q2, nRESET
  and and_3 (and_3_out, IOCLK, d_ff_2_qn, d_ff_3_qn);
  and and_4 (and_4_out, d_ff_2_qn, CLKS);
  or or_1 (or_1_out, and_3_out, and_4_out);
endmodule
