// Logisim project FAULTS_INT.circ as structural Verilog: 1 circuit, main circuit FAULTS_INT
module FAULTS_INT (
  input  nNP,
  input  MSWM,
  input  nNW,
  input  nBKPT,
  input  PRIV,
  input  MSWV,
  input  nTRAPO,
  input  nSYSCALL,
  input  CLKM,
  input  nDMA_REQ,
  input  MSWE,
  input  nNEXT0,
  input  CLKS,
  input  nCLR_TRAP,
  input  nIRQ0,
  input  nRESET,
  input  IOCLK,
  input  nIRQ1,
  input  nEL_FCODE,
  input  nIRQ2,
  input  nIRQ3,
  input  nIRQ4,
  input  nIRQ5,
  output FAULT_PENDING,
  output [3:0] ENCODER,
  output RL_FAULT,
  output [15:0] L
);

  wire ic_7474_1_q1, ic_7474_1_q2, ic_7474_2_q1, ic_7474_2_q2, ic_7474_3_q1, ic_7474_3_q2, ic_74138_1_y0,
       ic_74138_1_y1, ic_74138_1_y2, ic_74138_1_y3, ic_74138_1_y4, ic_74138_1_y5, ic_74138_1_y6,
       ic_74138_1_y7, ic_74273_1_y1, ic_74273_1_y2, ic_74273_1_y3, ic_74273_1_y4, ic_74273_2_y1,
       ic_74273_2_y2, ic_74273_2_y3, ic_74273_2_y4, ic_74273_2_y5, ic_74273_2_y6, ic_74273_2_y7,
       ic_74273_2_y8, not_1_out, not_2_out, not_3_out, not_4_out, not_5_out, not_6_out, not_7_out, not_8_out,
       U39E_out, U39F_out, U41C_out, U41D_out, U43B_out, U43C_out, U46_a0, U46_a1, U46_a2, U46_gs, U47_a0,
       U47_a1, U47_a2, U47_eo, U47_gs, U48C_out, U48D_out, U49A_out, U49C_out, U53A_out, U53B_out, U53C_out,
       U53D_out, U53E_out, U53F_out, U54A_out, U54B_out, U54C_out, U54D_out, U59A_out, U60D_out;

  not U53F (U53F_out, nNEXT0);
  or U49C (U49C_out, FAULT_PENDING, U53F_out);
  and U59B (RL_FAULT, U49C_out, CLKS);
  and U59A (U59A_out, nCLR_TRAP, nRESET);
  not U39D (ENCODER[3], U46_gs);
  nand U22D (ENCODER[2], U46_a2, U47_a2);
  nand U48B (ENCODER[1], U46_a1, U47_a1);
  nand U48A (ENCODER[0], U46_a0, U47_a0);
  IC_74273 ic_74273_1 (
    .Y2(ic_74273_1_y2), .Y3(ic_74273_1_y3), .Y1(ic_74273_1_y1), .Y4(ic_74273_1_y4), .D2(ENCODER[1]),
    .D3(ENCODER[2]), .D1(ENCODER[0]), .D4(ENCODER[3]), .D5(1'b0), .D6(1'b0), .D7(1'b0), .D8(1'b0),
    .CLK(RL_FAULT), .CLR(U59A_out));  // open: Y5, Y6, Y7, Y8
  IC_74244 ic_74244_1 (
    .Y3(L[5]), .Y4(L[4]), .Z1(L[3]), .Y1(L[7]), .Z2(L[2]), .Z3(L[1]), .Z4(L[0]), .Y2(L[6]), .A3(1'b0),
    .A4(1'b0), .OEA(nEL_FCODE), .B1(1'b0), .A1(1'b0), .B2(1'b0), .B3(1'b0), .B4(1'b0), .OEB(nEL_FCODE),
    .A2(1'b0));
  IC_74244 ic_74244_2 (
    .Y3(L[13]), .Y4(L[12]), .Z1(L[11]), .Y1(L[15]), .Z2(L[10]), .Z3(L[9]), .Z4(L[8]), .Y2(L[14]),
    .A3(ic_74273_1_y2), .A4(ic_74273_1_y3), .OEA(nEL_FCODE), .B1(ic_74273_1_y4), .A1(1'b0), .B2(1'b0),
    .B3(1'b0), .B4(1'b0), .OEB(nEL_FCODE), .A2(ic_74273_1_y1));
  and U60D (U60D_out, U59A_out, IOCLK);
  SN74148 U46 (
    .IN0(nSYSCALL), .IN1(1'b1), .IN2(U48C_out), .IN3(U48D_out), .IN4(nBKPT), .IN5(nNW), .IN6(nNP),
    .IN7(1'b1), .EI(1'b0), .EO(FAULT_PENDING), .GS(U46_gs), .A0(U46_a0), .A1(U46_a1), .A2(U46_a2));
  // NoConnect on U47_gs
  // NoConnect on U47_eo
  SN74148 U47 (
    .IN0(1'b1), .IN1(not_7_out), .IN2(not_6_out), .IN3(not_5_out), .IN4(not_4_out), .IN5(not_3_out),
    .IN6(not_2_out), .IN7(not_1_out), .EI(U49A_out), .EO(U47_eo), .GS(U47_gs), .A0(U47_a0), .A1(U47_a1),
    .A2(U47_a2));
  nor U43C (U43C_out, not_1_out, not_1_out);
  nor U43B (U43B_out, U43C_out, ic_74273_2_y1);
  or U49A (U49A_out, U43B_out, FAULT_PENDING);
  Pull_Resistor #(.pull(1)) pull_resistor_1 (.node(nIRQ0));
  Pull_Resistor #(.pull(1)) pull_resistor_2 (.node(nIRQ1));
  Pull_Resistor #(.pull(1)) pull_resistor_3 (.node(nIRQ2));
  Pull_Resistor #(.pull(1)) pull_resistor_4 (.node(nIRQ3));
  Pull_Resistor #(.pull(1)) pull_resistor_5 (.node(nIRQ4));
  Pull_Resistor #(.pull(1)) pull_resistor_6 (.node(nIRQ5));
  not U53D (U53D_out, nIRQ0);
  not U53C (U53C_out, nIRQ1);
  not U53B (U53B_out, nIRQ2);
  not U53A (U53A_out, nIRQ3);
  not U39F (U39F_out, nIRQ4);
  not U39E (U39E_out, nIRQ5);
  not not_1 (not_1_out, ic_74273_2_y8);
  not not_2 (not_2_out, ic_74273_2_y7);
  not not_3 (not_3_out, ic_74273_2_y6);
  not not_4 (not_4_out, ic_74273_2_y5);
  not not_5 (not_5_out, ic_74273_2_y4);
  not not_6 (not_6_out, ic_74273_2_y3);
  not not_7 (not_7_out, ic_74273_2_y2);
  IC_7474 ic_7474_1 (
    .Q2(ic_7474_1_q2), .Q1(ic_7474_1_q1), .CLK1(U53D_out), .CLR1(U54D_out), .SET2(1'b1), .D2(1'b1),
    .SET1(1'b1), .CLK2(U53C_out), .CLR2(U54C_out), .D1(1'b1));  // open: R1, R2
  IC_7474 ic_7474_2 (
    .Q2(ic_7474_2_q2), .Q1(ic_7474_2_q1), .CLK1(U53B_out), .CLR1(U54B_out), .SET2(1'b1), .D2(1'b1),
    .SET1(1'b1), .CLK2(U53A_out), .CLR2(U54A_out), .D1(1'b1));  // open: R1, R2
  IC_7474 ic_7474_3 (
    .Q2(ic_7474_3_q2), .Q1(ic_7474_3_q1), .CLK1(U39F_out), .CLR1(U41D_out), .SET2(1'b1), .D2(1'b1),
    .SET1(1'b1), .CLK2(U39E_out), .CLR2(U41C_out), .D1(1'b1));  // open: R1, R2
  IC_74273 ic_74273_2 (
    .Y2(ic_74273_2_y2), .Y3(ic_74273_2_y3), .Y1(ic_74273_2_y1), .Y4(ic_74273_2_y4), .Y5(ic_74273_2_y5),
    .Y6(ic_74273_2_y6), .Y7(ic_74273_2_y7), .Y8(ic_74273_2_y8), .D2(ic_7474_1_q1), .D3(ic_7474_1_q2),
    .D1(MSWE), .D4(ic_7474_2_q1), .D5(ic_7474_2_q2), .D6(ic_7474_3_q1), .D7(ic_7474_3_q2), .D8(not_8_out),
    .CLK(CLKM), .CLR(nRESET));
  and U54D (U54D_out, ic_74138_1_y6, nRESET);
  and U54C (U54C_out, ic_74138_1_y5, nRESET);
  and U54B (U54B_out, ic_74138_1_y4, nRESET);
  and U54A (U54A_out, ic_74138_1_y3, nRESET);
  and U41D (U41D_out, ic_74138_1_y2, nRESET);
  and U41C (U41C_out, ic_74138_1_y1, nRESET);
  nand U48D (U48D_out, MSWM, PRIV);
  nand U48C (U48C_out, MSWV, U53E_out);
  not not_8 (not_8_out, nDMA_REQ);
  not U53E (U53E_out, nTRAPO);
  Pull_Resistor #(.pull(1)) pull_resistor_7 (.node(nDMA_REQ));
  // NoConnect on ic_74138_1_y7
  // NoConnect on ic_74138_1_y0
  IC_74138 ic_74138_1 (
    .Y0(ic_74138_1_y0), .Y1(ic_74138_1_y1), .Y2(ic_74138_1_y2), .Y3(ic_74138_1_y3), .Y4(ic_74138_1_y4),
    .Y5(ic_74138_1_y5), .Y6(ic_74138_1_y6), .Y7(ic_74138_1_y7), .A2(ic_74273_1_y3), .A0(ic_74273_1_y1),
    .OE1(ic_74273_1_y4), .OE2(ic_74273_1_y4), .OE3(U60D_out), .A1(ic_74273_1_y2));

  // Notes on the sheet:
  //   Order of bits unclear in the schematics
  //   U52A
  //   U50B
  //   U51B
  //   U52B
endmodule
