// Logisim project Field_Decode.circ as structural Verilog: 1 circuit, main circuit Field_Decode
module Field_Decode (
  input  [7:0] IR,
  input  [3:0] EL,
  input  [3:0] LATCH,
  input  [3:0] FP_L,
  input  nSTOP_CLK,
  input  [3:0] MISC,
  input  [1:0] ER,
  input  nCLKS,
  input  CLKS,
  input  FAULT_PENDING,
  input  MSWM,
  input  LATCH_SZ,
  output RL_FPL,
  output nDO_RSHIFT,
  output nSYSCALL,
  output nDMA_ACK,
  output nHALT,
  output nDO_BRANCH,
  output nEL_MAR,
  output nBKPT,
  output nEL_MDR,
  output nEL_MSW,
  output nTRAPO,
  output nEL_SSP,
  output nEL_C,
  output nE_PTE,
  output nEL_TPC,
  output nEL_PC,
  output nSET_FLAGS,
  output nEL_FCODE,
  output nEL_DP,
  output nEL_SP,
  output XINIT_INST,
  output nER_MDR,
  output nEL_A,
  output nEL_B,
  output nER_IMM,
  output RCOMMIT,
  output R_L_PTE,
  output INIT_INST,
  output RL_IE,
  output nCLR_TRAP,
  output RL_MDR,
  output RL_PTB,
  output RL_MSW,
  output RL_C,
  output RL_PC,
  output RL_DP,
  output RL_SP,
  output RL_A_LO,
  output RL_B_LO,
  output RL_SSP,
  output RL_A_HI,
  output RL_B_HI
);

  wire not_1_out, not_10_out, U21B_out, U22C_out, U26_y0, U26_y1, U26_y2, U26_y3, U26_y4, U26_y5, U26_y6,
       U26_y7, U27_y0, U27_y1, U27_y2, U27_y3, U27_y4, U27_y5, U27_y6, U27_y7, U30_y1, U30_y5, U30_y6,
       U30_y7, U32_y2, U32_y4, U32_y5, U32_y6, U32_y7, U33_y0, U33_y7, U34_y1, U34_y2, U34_y3, U34_y4,
       U35_yeq, U36_y1, U36_y2, U36_y3, U36_y4, U37_y1, U37_y2, U37_y3, U37_y4, U38C_out, U39A_out, U40A_out,
       U41A_out, U42A_out, U43A_out, U44A_out, U60C_out;

  not not_1 (not_1_out, U36_y4);
  // NoConnect on U26_y7
  // NoConnect on U26_y6
  // NoConnect on U26_y5
  // NoConnect on U26_y4
  // NoConnect on U26_y3
  // NoConnect on U26_y2
  IC_74138 U26 (
    .Y0(U26_y0), .Y1(U26_y1), .Y2(U26_y2), .Y3(U26_y3), .Y4(U26_y4), .Y5(U26_y5), .Y6(U26_y6), .Y7(U26_y7),
    .A2(U36_y3), .A0(U36_y1), .OE1(not_1_out), .OE2(FAULT_PENDING), .OE3(CLKS), .A1(U36_y2));
  not not_2 (RL_MDR, U26_y0);
  not not_3 (RL_PTB, U26_y1);
  IC_74157 U36 (
    .Y2(U36_y2), .Y3(U36_y3), .Y4(U36_y4), .Y1(U36_y1), .A2(IR[6]), .B2(LATCH[2]), .A3(IR[5]), .B3(LATCH[1]),
    .A4(1'b0), .A1(IR[7]), .B4(LATCH[0]), .S0(U42A_out), .OE(1'b0), .B1(LATCH[3]));
  or U40C (RL_FPL, U44A_out, U60C_out);
  not U39A (U39A_out, MSWM);
  nand U42A (U42A_out, LATCH[3], LATCH[2], LATCH[1], LATCH[0]);
  and U44A (U44A_out, U43A_out, FP_L[3], FP_L[0]);
  and U60C (U60C_out, U35_yeq, nCLKS);
  not U39B (nER_IMM, ER[1]);
  nor U43A (U43A_out, FP_L[2], FP_L[1]);
  IC_7485 U35 (
    .YEQ(U35_yeq), .A3(U34_y3), .A4(U34_y4), .B1(FP_L[3]), .B2(FP_L[2]), .A1(U34_y1), .B3(FP_L[1]),
    .B4(FP_L[0]), .CLT(1'b0), .CEQ(1'b1), .CGT(1'b0), .A2(U34_y2));  // open: YLT, YGT
  IC_74138 U27 (
    .Y0(U27_y0), .Y1(U27_y1), .Y2(U27_y2), .Y3(U27_y3), .Y4(U27_y4), .Y5(U27_y5), .Y6(U27_y6), .Y7(U27_y7),
    .A2(U36_y3), .A0(U36_y1), .OE1(U36_y4), .OE2(FAULT_PENDING), .OE3(CLKS), .A1(U36_y2));
  // NoConnect on U27_y0
  not not_4 (RL_C, U27_y2);
  not not_5 (RL_PC, U27_y3);
  not not_6 (RL_DP, U27_y4);
  not not_7 (RL_SP, U27_y5);
  not not_8 (RL_A_LO, U27_y6);
  not not_9 (RL_B_LO, U27_y7);
  // NoConnect on U30_y7
  // NoConnect on U30_y6
  // NoConnect on U30_y5
  IC_74138 U30 (
    .Y0(nEL_MDR), .Y1(U30_y1), .Y2(nEL_SSP), .Y3(nEL_TPC), .Y4(nEL_FCODE), .Y5(U30_y5), .Y6(U30_y6),
    .Y7(U30_y7), .A2(U34_y3), .A0(U34_y1), .OE1(1'b0), .OE2(1'b0), .OE3(U34_y4), .A1(U34_y2));
  // NoConnect on U30_y1
  and U23D (RL_SSP, RL_SP, U39A_out);
  and U23B (RL_A_HI, RL_A_LO, LATCH_SZ);
  and U23C (RL_B_HI, RL_B_LO, LATCH_SZ);
  nand U22C (U22C_out, nSTOP_CLK, nDMA_ACK);
  IC_74157 U34 (
    .Y2(U34_y2), .Y3(U34_y3), .Y4(U34_y4), .Y1(U34_y1), .A2(U37_y2), .B2(FP_L[2]), .A3(U37_y3), .B3(FP_L[1]),
    .A4(U37_y4), .A1(U37_y1), .B4(FP_L[0]), .S0(U22C_out), .OE(1'b0), .B1(FP_L[3]));
  IC_74138 U31 (
    .Y0(nEL_MAR), .Y1(nEL_MSW), .Y2(nEL_C), .Y3(nEL_PC), .Y4(nEL_DP), .Y5(nEL_SP), .Y6(nEL_A), .Y7(nEL_B),
    .A2(U34_y3), .A0(U34_y1), .OE1(U34_y4), .OE2(1'b0), .OE3(1'b1), .A1(U34_y2));
  IC_74157 U37 (
    .Y2(U37_y2), .Y3(U37_y3), .Y4(U37_y4), .Y1(U37_y1), .A2(IR[6]), .B2(EL[2]), .A3(1'b1), .B3(EL[1]),
    .A4(1'b0), .A1(IR[7]), .B4(EL[0]), .S0(U21B_out), .OE(1'b0), .B1(EL[3]));
  // NoConnect on U32_y7
  // NoConnect on U32_y6
  IC_74138 U32 (
    .Y0(nDO_RSHIFT), .Y1(nDMA_ACK), .Y2(U32_y2), .Y3(nDO_BRANCH), .Y4(U32_y4), .Y5(U32_y5), .Y6(U32_y6),
    .Y7(U32_y7), .A2(MISC[1]), .A0(MISC[3]), .OE1(1'b0), .OE2(1'b0), .OE3(MISC[0]), .A1(MISC[2]));
  nand U21B (U21B_out, EL[3], EL[2], EL[1], EL[0]);
  IC_74138 U33 (
    .Y0(U33_y0), .Y1(nSYSCALL), .Y2(nHALT), .Y3(nBKPT), .Y4(nTRAPO), .Y5(nE_PTE), .Y6(nSET_FLAGS),
    .Y7(U33_y7), .A2(MISC[1]), .A0(MISC[3]), .OE1(MISC[0]), .OE2(1'b0), .OE3(1'b1), .A1(MISC[2]));
  // NoConnect on U33_y0
  nand U62D (XINIT_INST, U33_y7, U33_y7);
  and U41A (U41A_out, U33_y7, U32_y5);
  or U40B (R_L_PTE, nCLKS, nE_PTE);
  nor U38B (INIT_INST, nCLKS, U33_y7);
  nor U38A (RL_IE, nCLKS, U32_y2);
  or U40D (nCLR_TRAP, nCLKS, U32_y4);
  nor U38C (U38C_out, nCLKS, nSET_FLAGS);
  nor U38D (RCOMMIT, U41A_out, nCLKS);
  or U40A (U40A_out, U38C_out, U27_y1);
  not not_10 (not_10_out, FAULT_PENDING);
  and U41B (RL_MSW, U40A_out, not_10_out);

  assign nER_MDR = ER[1];
endmodule
