// Logisim project Field_Decode_2.circ as structural Verilog: 1 circuit, main circuit Field_Decode_2
module Field_Decode_2 (
  input  CLKS,
  input  RCOMMIT,
  input  RL_FPL,
  input  RL_PTB,
  input  XL_MODE,
  input  RL_A_HI,
  input  RL_B_HI,
  input  RL_SSP,
  input  XL_PAGING,
  input  RL_C,
  input  RL_PC,
  input  XL_MDR_LO,
  input  RL_DP,
  input  RL_SP,
  input  XL_MDR_HI,
  input  RL_A_LO,
  input  RL_B_LO,
  input  RL_MDR,
  input  RL_MSW,
  input  RL_IE,
  input  XL_MAR,
  input  R_L_PTE,
  input  RL_FAULT,
  input  R_RW,
  input  [1:0] RIMMVAL,
  input  FAULT_PENDING,
  output nCLKS,
  output COMMIT,
  output L_FPL,
  output L_PTB,
  output L_MODE,
  output L_A_HI,
  output L_B_HI,
  output L_PAGING,
  output L_SSP,
  output L_C,
  output L_PC,
  output L_MDR_LO,
  output L_DP,
  output L_SP,
  output L_MDR_HI,
  output L_A_LO,
  output L_B_LO,
  output L_MSW,
  output L_IE,
  output L_MAR,
  output nL_PTE,
  output L_FAULT,
  output nWR,
  output [1:0] IMMVAL,
  output n_RW
);

  wire U60A_out, U60B_out, U62A_out, U62B_out;

  and U59C (L_MODE, CLKS, XL_MODE);
  and U59D (L_PAGING, CLKS, XL_PAGING);
  and U60A (U60A_out, CLKS, XL_MDR_LO);
  and U60B (U60B_out, CLKS, XL_MDR_HI);
  nand U62C (nCLKS, CLKS, CLKS);
  nand U62A (U62A_out, CLKS, XL_MAR);
  nand U62B (U62B_out, CLKS, R_RW);
  or U49D (L_MDR_LO, U60A_out, RL_MDR);
  or U61A (L_MDR_HI, U60B_out, RL_MDR);
  or U43D (L_MAR, U62A_out, FAULT_PENDING);
  or U61C (nWR, U62B_out, FAULT_PENDING);
  buf buffer_1 (n_RW, R_RW);
  buf buffer_2 (COMMIT, RCOMMIT);
  buf buffer_3 (L_FPL, RL_FPL);
  buf buffer_4 (L_PTB, RL_PTB);
  buf buffer_5 (L_A_HI, RL_A_HI);
  buf buffer_6 (L_B_HI, RL_B_HI);
  buf buffer_7 (L_SSP, RL_SSP);
  buf buffer_8 (L_C, RL_C);
  buf buffer_9 (L_PC, RL_PC);
  buf buffer_10 (L_DP, RL_DP);
  buf buffer_11 (L_SP, RL_SP);
  buf buffer_12 (L_A_LO, RL_A_LO);
  buf buffer_13 (L_B_LO, RL_B_LO);
  buf buffer_14 (L_MSW, RL_MSW);
  buf buffer_15 (L_IE, RL_IE);
  buf buffer_16 (nL_PTE, R_L_PTE);
  buf buffer_17 (L_FAULT, RL_FAULT);
  assign IMMVAL = RIMMVAL;  // Buffer buffer_18, 2 bits wide
endmodule
