// Logisim project Front_Panel.circ as structural Verilog: 1 circuit, main circuit Front_Panel
module Front_Panel (
  input  nIRQ5,
  input  nIRQ4,
  input  nIRQ3,
  input  MSWP,
  input  nIRQ2,
  input  MSWE,
  input  nIRQ1,
  input  MSWM,
  input  MEMORY_IN,
  input  nIRQ0,
  input  MSWV,
  input  nHALT,
  input  MSWC,
  input  nRESET,
  input  MSWS,
  input  IDE_DRV,
  input  MSWZ,
  input  nRW,
  input  nPSEL2,
  input  [15:0] L,
  input  CLKS,
  input  L_FPL,
  input  XINIT_INST,
  input  [7:0] DBUS_IN,
  input  [7:0] IR,
  input  [15:0] MAR,
  input  nNP,
  input  nNW,
  input  MEMREF,
  input  nDMA_ACK,
  input  nWR,
  input  [21:0] A,
  input  INIT_INST,
  input  L_PCODE,
  output [1:0] CLOCK_SELECT,
  output nBP_RESET,
  output FP_RAM,
  output MEMORY_OUT,
  output nFP_WRITE,
  output [3:0] FP_L,
  output ZINIT_INST,
  output nDMA_REQ,
  output nSTOP_CLK,
  output [7:0] DBUS_OUT,
  output MANUAL_CLK
);

  wire BP_RESET_out, demultiplexer_1_out0, demultiplexer_1_out1, demultiplexer_1_out2, demultiplexer_1_out3,
       nand_1_out, nand_2_out, not_1_out, not_3_out, not_4_out, not_5_out, not_6_out, not_7_out, not_8_out,
       not_9_out, SEL_DEV_MEM;
  wire [5:1] not_12_out;
  wire [5:2] dipswitch_3_sw1;
  wire [7:0] dipswitch_4_sw1, U1_y8;
  wire [15:0] register_1_q;
  wire [21:0] dipswitch_1_sw1;

  not not_1 (not_1_out, nRESET);
  Register #(.width(16)) register_1 (.D(L), .en(1'b1), .clk(L_FPL), .Q(register_1_q), .clr(not_1_out));
  not not_2 (nBP_RESET, BP_RESET_out);
  Button BP_RESET (.out(BP_RESET_out));
  not not_3 (not_3_out, nIRQ5);
  not not_4 (not_4_out, nIRQ4);
  not not_5 (not_5_out, nIRQ3);
  not not_6 (not_6_out, nIRQ2);
  not not_7 (not_7_out, nIRQ1);
  not not_8 (not_8_out, nIRQ0);
  not not_9 (not_9_out, nHALT);
  not not_10 (not_12_out[5], nNP);
  not not_11 (not_12_out[4], nNW);
  not not_12 (not_12_out[1], nWR);
  LED IDE (.in(IDE_DRV));
  LED Reset (.in(not_1_out));
  LED L0 (.in(register_1_q[0]));
  LED L1 (.in(register_1_q[1]));
  LED P0 (.in(U1_y8[0]));
  LED P1 (.in(U1_y8[1]));
  LED IR0 (.in(IR[0]));
  LED IR1 (.in(IR[1]));
  LED IINIT (.in(INIT_INST));
  LED WR (.in(not_12_out[1]));
  LED A0 (.in(A[0]));
  LED A1 (.in(A[1]));
  LED Halt (.in(not_9_out));
  LED IRQ0 (.in(not_8_out));
  LED L2 (.in(register_1_q[2]));
  LED L3 (.in(register_1_q[3]));
  LED P2 (.in(U1_y8[2]));
  LED P3 (.in(U1_y8[3]));
  LED IR2 (.in(IR[2]));
  LED IR3 (.in(IR[3]));
  LED R_W (.in(nRW));
  LED Mref (.in(MEMREF));
  LED A2 (.in(A[2]));
  LED A3 (.in(A[3]));
  LED IRQ1 (.in(not_7_out));
  LED IRQ2 (.in(not_6_out));
  LED L4 (.in(register_1_q[4]));
  LED L5 (.in(register_1_q[5]));
  LED P4 (.in(U1_y8[4]));
  LED P5 (.in(U1_y8[5]));
  LED IR4 (.in(IR[4]));
  LED IR5 (.in(IR[5]));
  LED NW (.in(not_12_out[4]));
  LED NP (.in(not_12_out[5]));
  LED A4 (.in(A[4]));
  LED A5 (.in(A[5]));
  LED TURBO (.in(demultiplexer_1_out0));
  LED NORMAL (.in(demultiplexer_1_out1));
  LED SLOW (.in(demultiplexer_1_out2));
  LED MANUAL (.in(demultiplexer_1_out3));
  LED IRQ3 (.in(not_5_out));
  LED IRQ4 (.in(not_4_out));
  LED L6 (.in(register_1_q[6]));
  LED L7 (.in(register_1_q[7]));
  LED P6 (.in(U1_y8[6]));
  LED P7 (.in(U1_y8[7]));
  LED IR6 (.in(IR[6]));
  LED IR7 (.in(IR[7]));
  LED M0 (.in(MAR[0]));
  LED M1 (.in(MAR[1]));
  LED A6 (.in(A[6]));
  LED A7 (.in(A[7]));
  DipSwitch #(.number(22)) dipswitch_1 (
    .sw1(dipswitch_1_sw1[0]), .sw2(dipswitch_1_sw1[1]), .sw3(dipswitch_1_sw1[2]), .sw4(dipswitch_1_sw1[3]),
    .sw5(dipswitch_1_sw1[4]), .sw6(dipswitch_1_sw1[5]), .sw7(dipswitch_1_sw1[6]), .sw8(dipswitch_1_sw1[7]),
    .sw9(dipswitch_1_sw1[8]), .sw10(dipswitch_1_sw1[9]), .sw11(dipswitch_1_sw1[10]),
    .sw12(dipswitch_1_sw1[11]), .sw13(dipswitch_1_sw1[12]), .sw14(dipswitch_1_sw1[13]),
    .sw15(dipswitch_1_sw1[14]), .sw16(dipswitch_1_sw1[15]), .sw17(dipswitch_1_sw1[16]),
    .sw18(dipswitch_1_sw1[17]), .sw19(dipswitch_1_sw1[18]), .sw20(dipswitch_1_sw1[19]),
    .sw21(dipswitch_1_sw1[20]), .sw22(dipswitch_1_sw1[21]));
  Demultiplexer #(.enable("false"), .select(2)) demultiplexer_1 (
    .out0(demultiplexer_1_out0), .out1(demultiplexer_1_out1), .out2(demultiplexer_1_out2),
    .out3(demultiplexer_1_out3), .in(1'b1), .sel(CLOCK_SELECT));
  DipSwitch #(.number(3)) dipswitch_2 (.sw1(CLOCK_SELECT[1]), .sw2(CLOCK_SELECT[0]), .sw3(FP_RAM));
  LED IRQ5 (.in(not_3_out));
  LED P (.in(MSWP));
  LED L8 (.in(register_1_q[8]));
  LED L9 (.in(register_1_q[9]));
  LED Clock (.in(CLKS));
  LED Step (.in(MANUAL_CLK));
  LED M2 (.in(MAR[2]));
  LED M3 (.in(MAR[3]));
  LED A8 (.in(A[8]));
  LED A9 (.in(A[9]));
  LED E (.in(MSWE));
  LED M (.in(MSWM));
  LED L10 (.in(register_1_q[10]));
  LED L11 (.in(register_1_q[11]));
  LED Stop (.in(dipswitch_3_sw1[2]));
  LED Dev (.in(MEMORY_IN));
  Button button_1 (.out(MANUAL_CLK));
  LED M4 (.in(MAR[4]));
  LED M5 (.in(MAR[5]));
  LED A10 (.in(A[10]));
  LED A11 (.in(A[11]));
  LED C (.in(MSWC));
  LED V (.in(MSWV));
  LED L13 (.in(register_1_q[13]));
  LED L12 (.in(register_1_q[12]));
  Button Write (.out(dipswitch_3_sw1[5]));
  LED DMA (.in(dipswitch_3_sw1[4]));
  not not_13 (nSTOP_CLK, dipswitch_3_sw1[2]);
  DipSwitch #(.number(3)) dipswitch_3 (.sw1(dipswitch_3_sw1[2]), .sw2(SEL_DEV_MEM));  // open: sw3
  LED M7 (.in(MAR[7]));
  LED M6 (.in(MAR[6]));
  LED A13 (.in(A[13]));
  LED A12 (.in(A[12]));
  LED S (.in(MSWS));
  LED Z (.in(MSWZ));
  LED L14 (.in(register_1_q[14]));
  LED L15 (.in(register_1_q[15]));
  LED D0 (.in(DBUS_IN[0]));
  LED D1 (.in(DBUS_IN[1]));
  LED M8 (.in(MAR[8]));
  LED M9 (.in(MAR[9]));
  LED A14 (.in(A[14]));
  LED A15 (.in(A[15]));
  LED D2 (.in(DBUS_IN[2]));
  LED D3 (.in(DBUS_IN[3]));
  LED M10 (.in(MAR[10]));
  LED M11 (.in(MAR[11]));
  LED A16 (.in(A[16]));
  LED A17 (.in(A[17]));
  Pull_Resistor #(.pull(1)) pull_resistor_1 (.node(nDMA_REQ));
  LED D4 (.in(DBUS_IN[4]));
  LED D5 (.in(DBUS_IN[5]));
  DipSwitch dipswitch_4 (
    .sw1(dipswitch_4_sw1[0]), .sw2(dipswitch_4_sw1[1]), .sw3(dipswitch_4_sw1[2]), .sw4(dipswitch_4_sw1[3]),
    .sw5(dipswitch_4_sw1[4]), .sw6(dipswitch_4_sw1[5]), .sw7(dipswitch_4_sw1[6]), .sw8(dipswitch_4_sw1[7]));
  LED M12 (.in(MAR[12]));
  LED M13 (.in(MAR[13]));
  LED A18 (.in(A[18]));
  LED A19 (.in(A[19]));
  DipSwitch #(.number(4)) dipswitch_5 (.sw1(FP_L[0]), .sw2(FP_L[1]), .sw3(FP_L[2]), .sw4(FP_L[3]));
  LED D6 (.in(DBUS_IN[6]));
  LED D7 (.in(DBUS_IN[7]));
  LED M14 (.in(MAR[14]));
  LED M15 (.in(MAR[15]));
  LED A20 (.in(A[20]));
  LED A21 (.in(A[21]));
  not not_14 (nFP_WRITE, dipswitch_3_sw1[5]);
  assign DBUS_OUT = nand_2_out ? dipswitch_4_sw1 : 8'bz;  // Controlled_Buffer controlled_buffer_1
  assign A = dipswitch_3_sw1[4] ? dipswitch_1_sw1 : 22'bz;  // Controlled_Buffer controlled_buffer_2
  and and_1 (ZINIT_INST, CLKS, XINIT_INST);
  IC_74273 U1 (
    .Y2(U1_y8[6]), .Y3(U1_y8[5]), .Y1(U1_y8[7]), .Y4(U1_y8[4]), .Y5(U1_y8[3]), .Y6(U1_y8[2]), .Y7(U1_y8[1]),
    .Y8(U1_y8[0]), .D2(DBUS_IN[6]), .D3(DBUS_IN[5]), .D1(DBUS_IN[7]), .D4(DBUS_IN[4]), .D5(DBUS_IN[3]),
    .D6(DBUS_IN[2]), .D7(DBUS_IN[1]), .D8(DBUS_IN[0]), .CLK(L_PCODE), .CLR(1'b1));
  assign MEMORY_OUT = dipswitch_3_sw1[4] ? SEL_DEV_MEM : 1'bz;  // Controlled_Buffer controlled_buffer_3
  not not_15 (dipswitch_3_sw1[4], nDMA_ACK);
  nand nand_1 (nand_1_out, dipswitch_3_sw1[4], nRW);
  nand nand_2 (nand_2_out, nand_1_out, nPSEL2);

  // Notes on the sheet:
  //   Rear panel
  //   Front panel
  //   Clock speed
  //   Run
  //   Mem
  //   STEP
  //   Req
  //   0 MAR
  //   1 MDR
  //   2 DP
  //   3 FCODE
  //   4 C
  //   5 SSP
  //   6 A
  //   7 ---
  //   8 MSW
  //   9 ---
  //   A SP
  //   B ---
  //   C PC
  //   D TPC
  //   E B
  //   F ---
  //   Register Select
endmodule
