// Logisim project GREGS.circ as structural Verilog: 1 circuit, main circuit GREGS
module GREGS (
  input  [15:0] Z,
  input  L_A_HI,
  input  n_EL_A,
  input  L_A_LO,
  input  L_B_HI,
  input  n_EL_B,
  input  L_B_LO,
  input  nEL_C,
  input  L_C,
  input  nEL_DP,
  input  L_DP,
  input  nEL_SP,
  input  L_SP,
  input  nEL_SSP,
  input  L_SSP,
  input  nEL_PC,
  input  L_PC,
  input  nEL_TPC,
  input  COMMIT,
  input  nRESET,
  output [15:0] L
);

  wire not_1_out, not_2_out, not_3_out, not_4_out, not_5_out, not_6_out, not_7_out, not_8_out, not_9_out;
  wire [7:0] A_HI_q, A_LO_q, B_HI_q, B_LO_q;
  wire [15:0] C_q, DP_q, PC_q, SP_q, SSP_q, TPC_q;

  not not_1 (not_1_out, nRESET);
  Register A_HI (.D(Z[7:0]), .en(1'b1), .clk(L_A_HI), .Q(A_HI_q), .clr(not_1_out));
  not not_2 (not_2_out, n_EL_A);
  Register A_LO (.D(Z[15:8]), .en(1'b1), .clk(L_A_LO), .Q(A_LO_q), .clr(not_1_out));
  Register B_HI (.D(Z[7:0]), .en(1'b1), .clk(L_B_HI), .Q(B_HI_q), .clr(not_1_out));
  not not_3 (not_3_out, n_EL_B);
  Register B_LO (.D(Z[15:8]), .en(1'b1), .clk(L_B_LO), .Q(B_LO_q), .clr(not_1_out));
  not not_4 (not_4_out, nEL_C);
  Register #(.width(16)) C (.D(Z), .en(1'b1), .clk(L_C), .Q(C_q), .clr(not_1_out));
  not not_5 (not_5_out, nEL_DP);
  Register #(.width(16)) DP (.D(Z), .en(1'b1), .clk(L_DP), .Q(DP_q), .clr(not_1_out));
  not not_6 (not_6_out, nEL_SP);
  Register #(.width(16)) SP (.D(Z), .en(1'b1), .clk(L_SP), .Q(SP_q), .clr(not_1_out));
  not not_7 (not_7_out, nEL_SSP);
  Register #(.width(16)) SSP (.D(Z), .en(1'b1), .clk(L_SSP), .Q(SSP_q), .clr(not_1_out));
  not not_8 (not_8_out, nEL_PC);
  Register #(.width(16)) PC (.D(Z), .en(1'b1), .clk(L_PC), .Q(PC_q), .clr(not_1_out));
  Register #(.width(16)) TPC (.D(L), .en(1'b1), .clk(COMMIT), .Q(TPC_q), .clr(not_1_out));
  not not_9 (not_9_out, nEL_TPC);
  assign L[7:0] = not_2_out ? A_HI_q : 8'bz;  // Controlled_Buffer controlled_buffer_1
  assign L[15:8] = not_2_out ? A_LO_q : 8'bz;  // Controlled_Buffer controlled_buffer_2
  assign L[7:0] = not_3_out ? B_HI_q : 8'bz;  // Controlled_Buffer controlled_buffer_3
  assign L[15:8] = not_3_out ? B_LO_q : 8'bz;  // Controlled_Buffer controlled_buffer_4
  assign L = not_4_out ? C_q : 16'bz;  // Controlled_Buffer controlled_buffer_5
  assign L = not_5_out ? DP_q : 16'bz;  // Controlled_Buffer controlled_buffer_6
  assign L = not_6_out ? SP_q : 16'bz;  // Controlled_Buffer controlled_buffer_7
  assign L = not_7_out ? SSP_q : 16'bz;  // Controlled_Buffer controlled_buffer_8
  assign L = not_8_out ? PC_q : 16'bz;  // Controlled_Buffer controlled_buffer_9
  assign L = not_9_out ? TPC_q : 16'bz;  // Controlled_Buffer controlled_buffer_10
endmodule
