// Logisim project IR_DECODE.circ as structural Verilog: 1 circuit, main circuit IR_DECODE
module IR_DECODE (
  input  [1:0] CLOCK_SELECT,
  input  MANUAL_CLK,
  input  nFP_WRITE,
  input  nBP_RESET,
  input  [15:0] R,
  input  [3:0] FP_L,
  input  nSTOP_CLK,
  input  [15:0] MAR,
  input  nDMA_REQ,
  input  [5:0] nIRQ,
  output nRESET,
  output CLKS,
  output XINIT_INST,
  output INIT_INST,
  output nDMA_ACK,
  output IOCLK,
  output [7:0] IR,
  output [7:0] DBUS,
  output [15:0] Z,
  output [14:0] nEL_CTLBUS,
  output [7:0] MSW_FLAGS,
  output [5:0] xBUS,
  output COMMIT,
  output [15:0] T,
  output MEMREF,
  output nNW,
  output nNP,
  output [21:0] A,
  output [12:0] L_CTLBUS,
  output MEMORY,
  output nWR,
  output [1:0] IMMVAL,
  output [15:0] L,
  output nRW
);

  wire alu_1_aluc, alu_1_alus, alu_1_aluv, alu_1_aluz, clocks_1_clkm, faults_int_1_fault_pending,
       faults_int_1_rl_fault, field_decode_1_init_inst, field_decode_1_nclr_trap, field_decode_1_ndo_rshift,
       field_decode_1_nel_fcode, field_decode_1_nel_ssp, field_decode_1_ner_mdr, field_decode_1_nhalt,
       field_decode_1_nset_flags, field_decode_1_ntrapo, field_decode_1_r_l_pte, field_decode_1_rcommit,
       field_decode_1_rl_a_hi, field_decode_1_rl_a_lo, field_decode_1_rl_b_hi, field_decode_1_rl_b_lo,
       field_decode_1_rl_c, field_decode_1_rl_dp, field_decode_1_rl_ie, field_decode_1_rl_mdr,
       field_decode_1_rl_msw, field_decode_1_rl_pc, field_decode_1_rl_ptb, field_decode_1_rl_sp,
       field_decode_1_rl_ssp, field_decode_1_xinit_inst, field_decode_2_1_l_fault, field_decode_2_1_l_ie,
       field_decode_2_1_l_mode, field_decode_2_1_l_msw, field_decode_2_1_l_paging, field_decode_2_1_l_ptb,
       field_decode_2_1_nclks, field_decode_2_1_nl_pte, microcode_1_aluop_sz, microcode_1_code_ptb,
       microcode_1_latch_sz, microcode_1_ne_mdr_hi, microcode_1_nnext0, microcode_1_priv, microcode_1_r_rw,
       microcode_1_ruser_ptb, microcode_1_use_carry, microcode_1_xl_mar, microcode_1_xl_paging,
       page_table_1_nwait;
  wire [1:0] microcode_1_alu_op, microcode_1_er, microcode_1_rimm_val;
  wire [3:0] faults_int_1_encoder, microcode_1_el, microcode_1_latch, microcode_1_misc;

  CLOCKS clocks_1 (
    .CLOCK_SELECT(CLOCK_SELECT), .MANUAL_CLK(MANUAL_CLK), .nWAIT(page_table_1_nwait), .nSTOP_CLK(nSTOP_CLK),
    .nBP_RESET(nBP_RESET), .IOCLK(IOCLK), .CLKM(clocks_1_clkm), .CLKS(CLKS), .nRESET(nRESET));
  Field_Decode field_decode_1 (
    .RL_C(field_decode_1_rl_c), .RL_PC(field_decode_1_rl_pc), .RL_DP(field_decode_1_rl_dp),
    .RL_SP(field_decode_1_rl_sp), .RL_A_LO(field_decode_1_rl_a_lo), .RL_B_LO(field_decode_1_rl_b_lo),
    .RL_SSP(field_decode_1_rl_ssp), .RL_A_HI(field_decode_1_rl_a_hi), .RL_B_HI(field_decode_1_rl_b_hi),
    .nEL_MDR(nEL_CTLBUS[6]), .nEL_SSP(field_decode_1_nel_ssp), .nEL_TPC(nEL_CTLBUS[8]),
    .nEL_FCODE(field_decode_1_nel_fcode), .nEL_MAR(nEL_CTLBUS[5]), .nEL_MSW(xBUS[4]), .nEL_C(nEL_CTLBUS[7]),
    .nEL_PC(XINIT_INST), .nEL_DP(nEL_CTLBUS[11]), .nEL_SP(nEL_CTLBUS[12]), .nEL_A(nEL_CTLBUS[9]),
    .nEL_B(nEL_CTLBUS[10]), .nDO_RSHIFT(field_decode_1_ndo_rshift), .nDMA_ACK(nEL_CTLBUS[0]),
    .nDO_BRANCH(nEL_CTLBUS[1]), .nSYSCALL(nDMA_ACK), .nHALT(field_decode_1_nhalt), .nBKPT(nEL_CTLBUS[2]),
    .nTRAPO(field_decode_1_ntrapo), .nE_PTE(nEL_CTLBUS[3]), .nSET_FLAGS(field_decode_1_nset_flags),
    .INIT_INST(field_decode_1_init_inst), .RL_IE(field_decode_1_rl_ie), .nCLR_TRAP(field_decode_1_nclr_trap),
    .R_L_PTE(field_decode_1_r_l_pte), .XINIT_INST(field_decode_1_xinit_inst),
    .RCOMMIT(field_decode_1_rcommit), .RL_MSW(field_decode_1_rl_msw), .RL_MDR(field_decode_1_rl_mdr),
    .RL_PTB(field_decode_1_rl_ptb), .RL_FPL(INIT_INST), .nER_MDR(field_decode_1_ner_mdr),
    .nER_IMM(nEL_CTLBUS[4]), .LATCH(microcode_1_latch), .FP_L(FP_L), .nSTOP_CLK(nSTOP_CLK), .IR(IR),
    .EL(microcode_1_el), .MISC(microcode_1_misc), .FAULT_PENDING(faults_int_1_fault_pending),
    .nCLKS(field_decode_2_1_nclks), .MSWM(MSW_FLAGS[3]), .LATCH_SZ(microcode_1_latch_sz), .ER(microcode_1_er));
  FAULTS_INT faults_int_1 (
    .nNP(nNP), .MSWM(MSW_FLAGS[3]), .nNW(nNW), .nBKPT(field_decode_1_nclr_trap),
    .PRIV(microcode_1_xl_paging), .MSWV(MSW_FLAGS[4]), .nTRAPO(field_decode_1_nset_flags),
    .nSYSCALL(field_decode_1_ndo_rshift), .CLKM(clocks_1_clkm), .nDMA_REQ(nDMA_REQ), .MSWE(MSW_FLAGS[1]),
    .nNEXT0(microcode_1_nnext0), .CLKS(CLKS), .nCLR_TRAP(field_decode_1_rl_a_hi), .nIRQ0(nIRQ[0]),
    .nRESET(nRESET), .IOCLK(IOCLK), .nIRQ1(nIRQ[1]), .nEL_FCODE(field_decode_1_nel_ssp), .nIRQ2(nIRQ[2]),
    .nIRQ3(nIRQ[3]), .nIRQ4(nIRQ[4]), .nIRQ5(nIRQ[5]), .FAULT_PENDING(faults_int_1_fault_pending),
    .ENCODER(faults_int_1_encoder), .RL_FAULT(faults_int_1_rl_fault), .L(L));
  Microcode microcode_1 (
    .nNEXT0(microcode_1_nnext0), .EL(microcode_1_el), .ER(microcode_1_er), .RIMM_VAL(microcode_1_rimm_val),
    .ALUOP_SZ(microcode_1_aluop_sz), .ALU_OP(microcode_1_alu_op), .USE_CARRY(microcode_1_use_carry),
    .LATCH_SZ(microcode_1_latch_sz), .RUSER_PTB(microcode_1_ruser_ptb), .CODE_PTB(microcode_1_code_ptb),
    .LATCH(microcode_1_latch), .XL_MAR(microcode_1_xl_mar), .XL_MDR_LO(xBUS[4]), .XL_MDR_HI(xBUS[5]),
    .PRIV(microcode_1_priv), .XL_MODE(nEL_CTLBUS[13]), .XL_PAGING(microcode_1_xl_paging),
    .MISC(microcode_1_misc), .nE_MDR_LO(nEL_CTLBUS[14]), .nE_MDR_HI(microcode_1_ne_mdr_hi),
    .R_RW(microcode_1_r_rw), .IR(IR), .CLK_M(clocks_1_clkm), .nRESET(nRESET), .MSWC(MSW_FLAGS[6]),
    .MSWZ(MSW_FLAGS[7]), .MSWS(MSW_FLAGS[5]), .MSWV(MSW_FLAGS[4]), .nFP_WRITE(nFP_WRITE),
    .nDMA_ACQ(nDMA_ACK), .DBUS(DBUS), .INIT_INST(INIT_INST), .ENCODER(faults_int_1_encoder),
    .FAULT_PENDING(faults_int_1_fault_pending), .nDO_BRANCH(field_decode_1_nhalt));
  Field_Decode_2 field_decode_2_1 (
    .CLKS(CLKS), .RCOMMIT(field_decode_1_nel_fcode), .RL_FPL(field_decode_1_init_inst),
    .RL_PTB(field_decode_1_rl_ssp), .XL_MODE(microcode_1_ne_mdr_hi), .RL_A_HI(field_decode_1_r_l_pte),
    .RL_B_HI(field_decode_1_rl_mdr), .RL_SSP(field_decode_1_rl_ie), .XL_PAGING(microcode_1_priv),
    .RL_C(field_decode_1_rl_pc), .RL_PC(field_decode_1_rl_dp), .XL_MDR_LO(xBUS[4]),
    .RL_DP(field_decode_1_rl_sp), .RL_SP(field_decode_1_rl_a_lo), .XL_MDR_HI(xBUS[5]),
    .RL_A_LO(field_decode_1_rl_b_lo), .RL_B_LO(field_decode_1_rl_msw), .RL_MDR(field_decode_1_rl_b_hi),
    .RL_MSW(field_decode_1_rl_c), .RL_IE(field_decode_1_rl_ptb), .XL_MAR(microcode_1_r_rw),
    .R_L_PTE(field_decode_1_rcommit), .RL_FAULT(faults_int_1_rl_fault), .R_RW(microcode_1_xl_mar),
    .RIMMVAL(microcode_1_rimm_val), .FAULT_PENDING(faults_int_1_fault_pending),
    .nCLKS(field_decode_2_1_nclks), .COMMIT(COMMIT), .L_FPL(L_CTLBUS[0]), .L_PTB(field_decode_2_1_l_ptb),
    .L_MODE(field_decode_2_1_l_mode), .L_A_HI(L_CTLBUS[1]), .L_B_HI(L_CTLBUS[2]),
    .L_PAGING(field_decode_2_1_l_paging), .L_SSP(L_CTLBUS[3]), .L_C(L_CTLBUS[4]), .L_PC(L_CTLBUS[5]),
    .L_MDR_LO(L_CTLBUS[6]), .L_DP(L_CTLBUS[7]), .L_SP(L_CTLBUS[8]), .L_MDR_HI(L_CTLBUS[9]),
    .L_A_LO(L_CTLBUS[10]), .L_B_LO(L_CTLBUS[11]), .L_MSW(field_decode_2_1_l_msw),
    .L_IE(field_decode_2_1_l_ie), .L_MAR(L_CTLBUS[12]), .nL_PTE(field_decode_2_1_nl_pte),
    .L_FAULT(field_decode_2_1_l_fault), .nWR(nWR), .IMMVAL(IMMVAL), .n_RW(nRW));
  ALU alu_1 (
    .R(R), .L(L), .IR(IR), .ALU_OP(microcode_1_alu_op), .USE_CARRY(microcode_1_use_carry),
    .MSWC(MSW_FLAGS[6]), .ALUOP_SZ(microcode_1_aluop_sz), .nDO_RSHIFT(field_decode_1_xinit_inst),
    .ALUV(alu_1_aluv), .ALUC(alu_1_aluc), .ALUS(alu_1_alus), .ALUZ(alu_1_aluz), .Z(Z));  // open: Q
  MSW msw_1 (
    .ALUV(alu_1_aluv), .ALUS(alu_1_alus), .ALUC(alu_1_aluc), .ALUZ(alu_1_aluz), .Z(Z), .nSET_FLAGS(xBUS[4]),
    .L_FAULT(field_decode_2_1_l_fault), .MEMREF(MEMREF), .xCODE_PTB(xBUS[0]), .L_EI(field_decode_2_1_l_ie),
    .L_MSW(field_decode_2_1_l_msw), .nRESET(nRESET), .L_PAGING(field_decode_2_1_l_paging),
    .L_MODE(field_decode_2_1_l_mode), .nEL_MSW(field_decode_1_ntrapo), .MSWZ(MSW_FLAGS[7]),
    .MSWE(MSW_FLAGS[1]), .MSWC(MSW_FLAGS[6]), .MSWP(MSW_FLAGS[0]), .MSWS(MSW_FLAGS[5]), .MSWM(MSW_FLAGS[3]),
    .MSWV(MSW_FLAGS[4]), .L(L));
  PAGE_TABLE page_table_1 (
    .MAR(MAR), .nRESET(nRESET), .L_PTB(field_decode_2_1_l_ptb), .L_BUS(L), .nL_PTE(field_decode_2_1_nl_pte),
    .nE_PTE(field_decode_1_ner_mdr), .xMSWM(xBUS[1]), .xUSER_PTB(xBUS[2]), .MSWM(MSW_FLAGS[3]),
    .xMSWP(xBUS[3]), .MSWP(MSW_FLAGS[0]), .USER_PTB(microcode_1_ruser_ptb), .CODE_PTB(microcode_1_code_ptb),
    .L_MAR(L_CTLBUS[12]), .nRW(nRW), .XINIT_INST(XINIT_INST), .XL_MDR_LO(xBUS[4]), .XL_MDR_HI(xBUS[5]),
    .nE_MDR_LO(nEL_CTLBUS[13]), .nE_MDR_HI(nEL_CTLBUS[14]), .CLKM(clocks_1_clkm), .nDMA_ACK(nDMA_ACK), .T(T),
    .nWAIT(page_table_1_nwait), .MEMREF(MEMREF), .nNW(nNW), .nNP(nNP), .A_BUS(A), .MEMORY(MEMORY));  // open: F, M, W, P

  assign MSW_FLAGS[2] = 1'b0;
endmodule
