// Logisim project MDR.circ as structural Verilog: 1 circuit, main circuit MDR
module MDR (
  input  XL_MDR_HI,
  input  XL_MDR_LO,
  input  [15:0] Z,
  input  [7:0] D_IN,
  input  nE_MDR_HI,
  input  L_MDR_HI,
  input  nEL_MDR,
  input  nER_MDR,
  input  L_MDR_LO,
  input  COMMIT,
  input  nE_MDR_LO,
  output [7:0] D_OUT,
  output [15:0] L,
  output [15:0] R,
  output [15:0] out_15
);

  wire not_1_out, not_2_out, U12D_out, U51_y1, U51_y2, U51_y3, U51_y4, U52_y1, U52_y2, U52_y3, U52_y4,
       U62_y1, U62_y2, U63_y1, U63_y2, U64_y1, U64_y2, U65_y1, U65_y2;
  wire [15:0] U54_y1;

  IC_74153 U65 (
    .Y1(U65_y1), .Y2(U65_y2), .C1(1'b0), .D1(D_IN[0]), .A2(Z[1]), .A1(Z[0]), .B2(D_IN[1]), .C2(1'b0),
    .D2(D_IN[0]), .S0(XL_MDR_HI), .S1(XL_MDR_LO), .OE1(1'b0), .OE2(1'b0), .B1(D_IN[0]));
  IC_74153 U64 (
    .Y1(U64_y1), .Y2(U64_y2), .C1(1'b0), .D1(D_IN[0]), .A2(Z[3]), .A1(Z[2]), .B2(D_IN[3]), .C2(1'b0),
    .D2(D_IN[0]), .S0(XL_MDR_HI), .S1(XL_MDR_LO), .OE1(1'b0), .OE2(1'b0), .B1(D_IN[2]));
  IC_74153 U63 (
    .Y1(U63_y1), .Y2(U63_y2), .C1(1'b0), .D1(D_IN[0]), .A2(Z[5]), .A1(Z[4]), .B2(D_IN[5]), .C2(1'b0),
    .D2(D_IN[0]), .S0(XL_MDR_HI), .S1(XL_MDR_LO), .OE1(1'b0), .OE2(1'b0), .B1(D_IN[4]));
  IC_74153 U62 (
    .Y1(U62_y1), .Y2(U62_y2), .C1(1'b0), .D1(D_IN[0]), .A2(Z[7]), .A1(Z[6]), .B2(D_IN[7]), .C2(1'b0),
    .D2(D_IN[0]), .S0(XL_MDR_HI), .S1(XL_MDR_LO), .OE1(1'b0), .OE2(1'b0), .B1(D_IN[6]));
  IC_74157 U52 (
    .Y2(U52_y2), .Y3(U52_y3), .Y4(U52_y4), .Y1(U52_y1), .A2(Z[9]), .B2(D_IN[1]), .A3(Z[10]), .B3(D_IN[2]),
    .A4(Z[11]), .A1(Z[8]), .B4(D_IN[3]), .S0(XL_MDR_LO), .OE(1'b0), .B1(D_IN[0]));
  IC_74157 U51 (
    .Y2(U51_y2), .Y3(U51_y3), .Y4(U51_y4), .Y1(U51_y1), .A2(Z[13]), .B2(D_IN[5]), .A3(Z[14]), .B3(D_IN[6]),
    .A4(Z[15]), .A1(Z[12]), .B4(D_IN[7]), .S0(XL_MDR_LO), .OE(1'b0), .B1(D_IN[4]));
  not U12D (U12D_out, COMMIT);
  IC_74273 U54 (
    .Y2(U54_y1[1]), .Y3(U54_y1[2]), .Y1(U54_y1[0]), .Y4(U54_y1[3]), .Y5(U54_y1[4]), .Y6(U54_y1[5]),
    .Y7(U54_y1[6]), .Y8(U54_y1[7]), .D2(U65_y2), .D3(U64_y1), .D1(U65_y1), .D4(U64_y2), .D5(U63_y1),
    .D6(U63_y2), .D7(U62_y1), .D8(U62_y2), .CLK(L_MDR_HI), .CLR(U12D_out));
  IC_74273 U53 (
    .Y2(U54_y1[9]), .Y3(U54_y1[10]), .Y1(U54_y1[8]), .Y4(U54_y1[11]), .Y5(U54_y1[12]), .Y6(U54_y1[13]),
    .Y7(U54_y1[14]), .Y8(U54_y1[15]), .D2(U52_y2), .D3(U52_y3), .D1(U52_y1), .D4(U52_y4), .D5(U51_y1),
    .D6(U51_y2), .D7(U51_y3), .D8(U51_y4), .CLK(L_MDR_LO), .CLR(U12D_out));
  IC_74244 U55 (
    .Y3(D_OUT[2]), .Y4(D_OUT[3]), .Z1(D_OUT[4]), .Y1(D_OUT[0]), .Z2(D_OUT[5]), .Z3(D_OUT[6]), .Z4(D_OUT[7]),
    .Y2(D_OUT[1]), .A3(U54_y1[2]), .A4(U54_y1[3]), .OEA(nE_MDR_HI), .B1(U54_y1[4]), .A1(U54_y1[0]),
    .B2(U54_y1[5]), .B3(U54_y1[6]), .B4(U54_y1[7]), .OEB(nE_MDR_HI), .A2(U54_y1[1]));
  IC_74244 U56 (
    .Y3(D_OUT[2]), .Y4(D_OUT[3]), .Z1(D_OUT[4]), .Y1(D_OUT[0]), .Z2(D_OUT[5]), .Z3(D_OUT[6]), .Z4(D_OUT[7]),
    .Y2(D_OUT[1]), .A3(U54_y1[10]), .A4(U54_y1[11]), .OEA(nE_MDR_LO), .B1(U54_y1[12]), .A1(U54_y1[8]),
    .B2(U54_y1[13]), .B3(U54_y1[14]), .B4(U54_y1[15]), .OEB(nE_MDR_LO), .A2(U54_y1[9]));
  assign L = not_1_out ? U54_y1 : 16'bz;  // Controlled_Buffer U59_60
  not not_1 (not_1_out, nEL_MDR);
  assign R = not_2_out ? U54_y1 : 16'bz;  // Controlled_Buffer U57_58
  not not_2 (not_2_out, nER_MDR);
  REVERSE16 reverse16_1 (.MY_IN(U54_y1), .MY_OUT(out_15));

  // Notes on the sheet:
  //   Unused inputs to GND
endmodule
