// Logisim project MSW.circ as structural Verilog: 1 circuit, main circuit main
module main (
  input  ALUV,
  input  ALUS,
  input  ALUC,
  input  ALUZ,
  input  [15:0] Z,
  input  nSET_FLAGS,
  input  L_FAULT,
  input  MEMREF,
  input  xCODE_PTB,
  input  L_EI,
  input  L_MSW,
  input  nRESET,
  input  L_PAGING,
  input  L_MODE,
  input  nEL_MSW,
  output MSWZ,
  output MSWE,
  output MSWC,
  output MSWP,
  output MSWS,
  output MSWM,
  output MSWV,
  output [15:0] L
);

  wire not_1_out, U12C_out, U19B_out, U23_pin4, U23_pin6, U23_pin8, U24_pin6, U24_pin8, U26_pin12, U26_pin13,
       U26_pin14, U26_pin15, U26_pin16, U26_pin17, U26_pin18, U26_pin19;
  wire [3:0] multiplexer_1_out;
  wire [10:10] U24_pin9;

  _7474 U23 (
    .pin1(nRESET), .pin2(Z[8]), .pin3(L_PAGING), .pin4(U23_pin4), .pin5(MSWP), .pin6(U23_pin6),
    .pin13(nRESET), .pin12(Z[9]), .pin11(L_EI), .pin10(U23_pin4), .pin9(MSWE), .pin8(U23_pin8));
  // NoConnect on U23_pin6
  and U19B (U19B_out, L_FAULT, MEMREF);
  // NoConnect on U23_pin8
  not U12C (U12C_out, L_MODE);
  _7474 U24 (
    .pin1(nRESET), .pin2(Z[11]), .pin3(L_MODE), .pin4(U23_pin4), .pin5(MSWM), .pin6(U24_pin6),
    .pin13(U12C_out), .pin12(xCODE_PTB), .pin11(U19B_out), .pin10(U23_pin4), .pin9(U24_pin9[10]),
    .pin8(U24_pin8));
  not not_1 (not_1_out, nEL_MSW);
  // NoConnect on U24_pin6
  assign L = not_1_out ? {MSWZ, MSWC, MSWS, MSWV, MSWM, U24_pin9[10], MSWE, MSWP, {8{1'b0}}} : 16'bz;  // Controlled_Buffer controlled_buffer_1
  // NoConnect on U24_pin8
  Multiplexer #(.enable("false"), .width(4)) multiplexer_1 (
    .in0({ALUZ, ALUC, ALUS, ALUV}), .in1(Z[15:12]), .out(multiplexer_1_out), .sel(nSET_FLAGS));
  // NoConnect on U26_pin19
  // NoConnect on U26_pin18
  // NoConnect on U26_pin17
  _74273 U26 (
    .pin1(nRESET), .pin2(MSWZ), .pin3(multiplexer_1_out[3]), .pin4(multiplexer_1_out[2]), .pin5(MSWC),
    .pin6(MSWS), .pin7(multiplexer_1_out[1]), .pin8(multiplexer_1_out[0]), .pin9(MSWV), .pin19(U26_pin19),
    .pin18(U26_pin18), .pin17(U26_pin17), .pin16(U26_pin16), .pin15(U26_pin15), .pin14(U26_pin14),
    .pin13(U26_pin13), .pin12(U26_pin12), .pin11(L_MSW));
  // NoConnect on U26_pin16
  // NoConnect on U26_pin15
  // NoConnect on U26_pin14
  // NoConnect on U26_pin13
  // NoConnect on U26_pin12
  // also tied to VCC on the sheet: U23_pin4
endmodule
