// Logisim project Magic1_TTL.circ as structural Verilog: 9 circuits, main circuit SN74381
module SN74381 (
  input  Cn,
  input  B0,
  input  A0,
  input  B1,
  input  A1,
  input  B2,
  input  A2,
  input  B3,
  input  A3,
  input  S0,
  input  S1,
  input  S2,
  output F0,
  output F1,
  output F2,
  output F3,
  output nP,
  output nG
);

  wire and_1_out, and_2_out, and_3_out, and_4_out, and_5_out, and_6_out, and_7_out, and_8_out, and_9_out,
       and_10_out, and_11_out, and_12_out, and_13_out, and_14_out, and_15_out, and_16_out, and_17_out,
       and_18_out, and_19_out, and_20_out, and_21_out, and_22_out, and_23_out, and_24_out, and_25_out,
       and_26_out, and_27_out, and_28_out, and_29_out, and_30_out, and_31_out, and_32_out, and_33_out,
       and_34_out, and_35_out, and_36_out, and_37_out, and_38_out, and_39_out, and_40_out, and_41_out,
       and_42_out, and_43_out, and_44_out, nand_1_out, nand_2_out, nand_3_out, nand_4_out, nand_6_out,
       nor_1_out, nor_2_out, nor_3_out, nor_4_out, nor_5_out, nor_6_out, nor_7_out, nor_8_out, nor_9_out,
       nor_10_out, nor_11_out, nor_12_out, not_1_out, not_2_out, not_3_out, not_4_out, not_5_out, not_6_out,
       not_7_out, not_8_out, not_9_out, not_10_out, not_11_out, not_12_out, not_13_out, not_14_out;

  not not_1 (not_1_out, B0);
  not not_2 (not_2_out, A0);
  not not_3 (not_3_out, B1);
  not not_4 (not_4_out, A1);
  not not_5 (not_5_out, B2);
  not not_6 (not_6_out, A2);
  not not_7 (not_7_out, B3);
  not not_8 (not_8_out, A3);
  not not_9 (not_9_out, S0);
  not not_10 (not_10_out, S1);
  not not_11 (not_11_out, S2);
  not not_12 (not_12_out, not_9_out);
  not not_13 (not_13_out, not_10_out);
  not not_14 (not_14_out, not_11_out);
  nand nand_1 (nand_1_out, not_9_out, not_10_out);
  nand nand_2 (nand_2_out, not_10_out, not_11_out);
  and and_1 (and_1_out, nand_2_out, nand_3_out, not_1_out, not_2_out);
  and and_2 (and_2_out, nand_1_out, nand_3_out, nand_4_out, not_1_out, A0);
  and and_3 (and_3_out, nand_2_out, nand_4_out, B0, not_2_out);
  and and_4 (and_4_out, nand_1_out, nand_4_out, not_1_out, not_2_out, nor_9_out);
  and and_5 (and_5_out, nand_2_out, nand_3_out, not_1_out, A0);
  and and_6 (and_6_out, nand_2_out, nand_3_out, B0, not_2_out);
  and and_7 (and_7_out, nand_1_out, nand_4_out, B0, A0);
  and and_8 (and_8_out, nand_2_out, nand_3_out, not_3_out, not_4_out);
  and and_9 (and_9_out, nand_1_out, nand_3_out, nand_4_out, not_3_out, A1);
  and and_10 (and_10_out, nand_2_out, nand_4_out, B1, not_4_out);
  and and_11 (and_11_out, nand_1_out, nand_4_out, nor_9_out, not_3_out, not_4_out);
  and and_12 (and_12_out, nand_2_out, nand_3_out, not_3_out, A1);
  and and_13 (and_13_out, nand_2_out, nand_3_out, B1, not_4_out);
  and and_14 (and_14_out, nand_1_out, nand_4_out, B1, A1);
  and and_15 (and_15_out, nand_2_out, nand_3_out, not_5_out, not_6_out);
  and and_16 (and_16_out, nand_1_out, nand_3_out, nand_4_out, not_5_out, A2);
  and and_17 (and_17_out, nand_2_out, nand_4_out, B2, not_6_out);
  and and_18 (and_18_out, nand_1_out, nand_4_out, nor_9_out, not_5_out, not_6_out);
  and and_19 (and_19_out, nand_2_out, nand_3_out, not_5_out, A2);
  and and_20 (and_20_out, nand_2_out, nand_3_out, B2, not_6_out);
  and and_21 (and_21_out, nand_1_out, nand_4_out, B2, A2);
  and and_22 (and_22_out, nand_2_out, nand_3_out, not_7_out, not_8_out);
  and and_23 (and_23_out, nand_1_out, nand_3_out, nand_4_out, not_7_out, A3);
  and and_24 (and_24_out, nand_2_out, nand_4_out, B3, not_8_out);
  and and_25 (and_25_out, nand_1_out, nand_4_out, nor_9_out, not_7_out, not_8_out);
  and and_26 (and_26_out, nand_2_out, nand_3_out, not_7_out, A3);
  and and_27 (and_27_out, nand_2_out, nand_3_out, B3, not_8_out);
  and and_28 (and_28_out, nand_1_out, nand_4_out, B3, A3);
  nand nand_3 (nand_3_out, not_9_out, not_13_out);
  nand nand_4 (nand_4_out, not_12_out, not_13_out, not_11_out);
  and and_29 (and_29_out, not_10_out, not_14_out);
  nor nor_1 (nor_1_out, and_1_out, and_2_out, and_3_out);
  nor nor_2 (nor_2_out, and_4_out, and_5_out, and_6_out, and_7_out);
  nor nor_3 (nor_3_out, and_8_out, and_9_out, and_10_out);
  nor nor_4 (nor_4_out, and_11_out, and_12_out, and_13_out, and_14_out);
  nor nor_5 (nor_5_out, and_15_out, and_16_out, and_17_out);
  nor nor_6 (nor_6_out, and_18_out, and_19_out, and_20_out, and_21_out);
  nor nor_7 (nor_7_out, and_22_out, and_23_out, and_24_out);
  nor nor_8 (nor_8_out, and_25_out, and_26_out, and_27_out, and_28_out);
  and and_30 (and_30_out, nand_1_out, not_11_out);
  and and_31 (and_31_out, not_9_out, not_14_out);
  nor nor_9 (nor_9_out, and_31_out, and_29_out);
  and and_32 (and_32_out, Cn, nor_1_out, and_30_out);
  and and_33 (and_33_out, nor_1_out, nor_2_out, and_30_out);
  and and_34 (and_34_out, Cn, nor_1_out, nor_3_out, and_30_out);
  and and_35 (and_35_out, nor_1_out, nor_3_out, nor_2_out, and_30_out);
  and and_36 (and_36_out, nor_3_out, nor_4_out, and_30_out);
  and and_37 (and_37_out, Cn, nor_1_out, nor_3_out, nor_5_out, and_30_out);
  and and_38 (and_38_out, nor_1_out, nor_3_out, nor_5_out, nor_2_out, and_30_out);
  and and_39 (and_39_out, nor_3_out, nor_5_out, nor_4_out, and_30_out);
  and and_40 (and_40_out, nor_5_out, nor_6_out, and_30_out);
  nand nand_5 (nP, nor_1_out, nor_3_out, nor_5_out, nor_7_out);
  and and_41 (and_41_out, nor_1_out, nor_3_out, nor_5_out, nor_7_out, nor_2_out);
  and and_42 (and_42_out, nor_3_out, nor_5_out, nor_7_out, nor_4_out);
  and and_43 (and_43_out, nor_5_out, nor_7_out, nor_6_out);
  and and_44 (and_44_out, nor_7_out, nor_8_out);
  nand nand_6 (nand_6_out, Cn, and_30_out);
  nor nor_10 (nor_10_out, and_32_out, and_33_out);
  nor nor_11 (nor_11_out, and_34_out, and_35_out, and_36_out);
  nor nor_12 (nor_12_out, and_37_out, and_38_out, and_39_out, and_40_out);
  nor nor_13 (nG, and_41_out, and_42_out, and_43_out, and_44_out);
  xor xor_1 (F0, nand_6_out, nor_2_out);
  xor xor_2 (F1, nor_10_out, nor_4_out);
  xor xor_3 (F2, nor_11_out, nor_6_out);
  xor xor_4 (F3, nor_12_out, nor_8_out);
  Hex_Digit_Display hex_digit_display_1 (.value({F3, F2, F1, F0}));  // open: dp
endmodule

module SN74182 (
  input  nP3,
  input  nG3,
  input  nP2,
  input  nG2,
  input  nP1,
  input  nG1,
  input  nP0,
  input  nG0,
  input  Cn,
  output nP,
  output nG,
  output Cnz,
  output Cny,
  output Cnx
);

  wire and_1_out, and_2_out, and_3_out, and_4_out, and_5_out, and_6_out, and_7_out, and_8_out, and_9_out,
       and_10_out, and_11_out, and_12_out, and_13_out, not_1_out;

  not not_1 (not_1_out, Cn);
  or or_1 (nP, nP3, nP2, nP1, nP0);
  and and_1 (and_1_out, nG3, nG2, nG1, nG0);
  and and_2 (and_2_out, nP1, nG3, nG2, nG1);
  and and_3 (and_3_out, nP2, nG3, nG2);
  and and_4 (and_4_out, nP3, nG3);
  and and_5 (and_5_out, nG2, nG1, nG0, not_1_out);
  and and_6 (and_6_out, nP0, nG2, nG1, nG0);
  and and_7 (and_7_out, nP1, nG2, nG1);
  and and_8 (and_8_out, nP2, nG2);
  and and_9 (and_9_out, nG1, nG0, not_1_out);
  and and_10 (and_10_out, nP0, nG1, nG0);
  and and_11 (and_11_out, nP1, nG1);
  and and_12 (and_12_out, nG0, not_1_out);
  and and_13 (and_13_out, nP0, nG0);
  or or_2 (nG, and_1_out, and_2_out, and_3_out, and_4_out);
  nor nor_1 (Cnz, and_5_out, and_6_out, and_7_out, and_8_out);
  nor nor_2 (Cny, and_9_out, and_10_out, and_11_out);
  nor nor_3 (Cnx, and_12_out, and_13_out);
endmodule

module SN74148 (
  input  IN0,
  input  IN1,
  input  IN2,
  input  IN3,
  input  IN4,
  input  IN5,
  input  IN6,
  input  IN7,
  input  EI,
  output EO,
  output GS,
  output A0,
  output A1,
  output A2
);

  wire and_1_out, and_2_out, and_3_out, and_4_out, and_5_out, and_6_out, and_7_out, and_8_out, and_9_out,
       and_10_out, and_11_out, and_12_out, not_1_out, not_2_out, not_3_out, not_4_out, not_5_out, not_6_out,
       not_7_out, not_8_out, not_9_out, not_10_out, not_11_out, not_12_out;

  not not_1 (not_1_out, IN1);
  not not_2 (not_2_out, IN2);
  not not_3 (not_3_out, IN3);
  not not_4 (not_4_out, IN4);
  not not_5 (not_5_out, IN5);
  not not_6 (not_6_out, IN6);
  not not_7 (not_7_out, IN7);
  not not_8 (not_8_out, EI);
  not not_9 (not_9_out, not_2_out);
  not not_10 (not_10_out, not_4_out);
  not not_11 (not_11_out, not_5_out);
  not not_12 (not_12_out, not_6_out);
  nand nand_1 (EO, IN0, IN1, IN2, IN3, IN4, IN5, IN6, IN7, not_8_out);
  and and_1 (and_1_out, not_1_out, not_9_out, not_10_out, not_12_out, not_8_out);
  and and_2 (and_2_out, not_3_out, not_10_out, not_12_out, not_8_out);
  and and_3 (and_3_out, not_5_out, not_12_out, not_8_out);
  and and_4 (and_4_out, not_7_out, not_8_out);
  and and_5 (and_5_out, not_2_out, not_10_out, not_11_out, not_8_out);
  and and_6 (and_6_out, not_3_out, not_10_out, not_11_out, not_8_out);
  and and_7 (and_7_out, not_6_out, not_8_out);
  and and_8 (and_8_out, not_7_out, not_8_out);
  and and_9 (and_9_out, not_4_out, not_8_out);
  and and_10 (and_10_out, not_5_out, not_8_out);
  and and_11 (and_11_out, not_6_out, not_8_out);
  and and_12 (and_12_out, not_7_out, not_8_out);
  nand nand_2 (GS, EO, not_8_out);
  nor nor_1 (A0, and_1_out, and_2_out, and_3_out, and_4_out);
  nor nor_2 (A1, and_5_out, and_6_out, and_7_out, and_8_out);
  nor nor_3 (A2, and_9_out, and_10_out, and_11_out, and_12_out);
endmodule

module SN74245 (
  input  nG,
  input  DIR,
  output [7:0] A,
  output [7:0] B
);

  wire and_1_out, and_2_out, not_1_out, not_2_out;

  not not_1 (not_1_out, nG);
  not not_2 (not_2_out, DIR);
  and and_1 (and_1_out, not_1_out, DIR);
  and and_2 (and_2_out, not_1_out, not_2_out);
  assign B = and_1_out ? A : 8'bz;  // Controlled_Buffer controlled_buffer_1
  assign A = and_2_out ? B : 8'bz;  // Controlled_Buffer controlled_buffer_2
endmodule

module RAM62256 (
  input  nWE,
  input  [14:0] A,
  input  nOE,
  input  nCS,
  input  [7:0] D_IN,
  output [7:0] D_OUT
);

  wire and_1_out, and_2_out, not_1_out, not_2_out, not_3_out;
  wire [7:0] U2_dout;

  not not_1 (not_1_out, nWE);
  not not_2 (not_2_out, nOE);
  not not_3 (not_3_out, nCS);
  and and_1 (and_1_out, not_1_out, not_3_out);
  and and_2 (and_2_out, not_2_out, not_3_out);
  RAM #(.addrWidth(15), .trigger("high")) U2 (.addr(A), .we(and_1_out), .oe(and_2_out), .din(D_IN), .dout(U2_dout));
  assign D_OUT = and_2_out ? U2_dout : 8'bz;  // Controlled_Buffer controlled_buffer_1
endmodule

module ROM27256 (
  input  [14:0] A,
  input  nCS,
  input  nOE,
  output [7:0] D
);

  wire and_1_out, not_1_out, not_2_out;
  wire [7:0] BIOS_data;

  ROM #(.addrWidth(15)) BIOS (.addr(A), .data(BIOS_data));
  not not_1 (not_1_out, nCS);
  not not_2 (not_2_out, nOE);
  and and_1 (and_1_out, not_1_out, not_2_out);
  assign D = and_1_out ? BIOS_data : 8'bz;  // Controlled_Buffer controlled_buffer_1

  // Notes on the sheet:
  //   contents of BIOS (hex, n*v repeats v):
  //   32768*66
endmodule

module SN74382 (
  input  Cn,
  input  A0,
  input  B0,
  input  A1,
  input  B1,
  input  A2,
  input  B2,
  input  A3,
  input  B3,
  input  S0,
  input  S1,
  input  S2,
  output F0,
  output F1,
  output F2,
  output F3,
  output OVR,
  output Cn4
);

  wire and_1_out, and_2_out, and_3_out, and_4_out, and_5_out, and_6_out, and_7_out, and_8_out, and_9_out,
       and_10_out, and_11_out, and_12_out, and_13_out, and_14_out, and_15_out, and_16_out, and_17_out,
       and_18_out, and_19_out, and_20_out, and_21_out, and_22_out, and_23_out, and_24_out, and_25_out,
       and_26_out, and_27_out, and_28_out, and_29_out, and_30_out, and_31_out, and_32_out, and_33_out,
       and_34_out, and_35_out, and_36_out, and_37_out, and_38_out, and_39_out, and_40_out, and_41_out,
       and_42_out, and_43_out, and_44_out, and_45_out, nand_1_out, nand_2_out, nand_3_out, nand_4_out,
       nand_5_out, nand_6_out, nor_1_out, nor_2_out, nor_3_out, nor_4_out, nor_5_out, nor_6_out, nor_7_out,
       nor_8_out, nor_9_out, nor_10_out, nor_11_out, nor_12_out, nor_13_out, nor_14_out, not_1_out,
       not_2_out, not_3_out, not_4_out, not_5_out, not_6_out, not_7_out, not_8_out, not_9_out, not_10_out,
       not_11_out, not_12_out, not_13_out, not_14_out;

  not not_1 (not_1_out, S0);
  not not_2 (not_2_out, S1);
  not not_3 (not_3_out, S2);
  not not_4 (not_4_out, A0);
  not not_5 (not_5_out, B0);
  not not_6 (not_6_out, A1);
  not not_7 (not_7_out, B1);
  not not_8 (not_8_out, A2);
  not not_9 (not_9_out, B2);
  not not_10 (not_10_out, A3);
  not not_11 (not_11_out, B3);
  nand nand_1 (nand_1_out, not_1_out, not_2_out);
  not not_12 (not_12_out, not_1_out);
  nand nand_2 (nand_2_out, not_2_out, not_3_out);
  not not_13 (not_13_out, not_2_out);
  not not_14 (not_14_out, not_3_out);
  and and_1 (and_1_out, not_4_out, not_5_out, nand_3_out, nand_2_out);
  and and_2 (and_2_out, nand_1_out, nand_3_out, nand_4_out, A0, not_5_out);
  and and_3 (and_3_out, nand_2_out, nand_4_out, not_4_out, B0);
  and and_4 (and_4_out, not_4_out, not_5_out, nand_1_out, nand_4_out, nor_9_out);
  and and_5 (and_5_out, nand_2_out, nand_3_out, A0, not_5_out);
  and and_6 (and_6_out, nand_2_out, nand_3_out, not_4_out, B0);
  and and_7 (and_7_out, nand_1_out, nand_4_out, A0, B0);
  and and_8 (and_8_out, not_6_out, not_7_out, nand_3_out, nand_2_out);
  and and_9 (and_9_out, nand_2_out, nand_3_out, nand_4_out, A1, not_7_out);
  and and_10 (and_10_out, nand_2_out, nand_4_out, not_6_out, B1);
  and and_11 (and_11_out, not_6_out, not_7_out, nand_1_out, nand_4_out, nor_9_out);
  and and_12 (and_12_out, nand_2_out, nand_3_out, A1, not_7_out);
  and and_13 (and_13_out, nand_2_out, nand_3_out, not_6_out, B1);
  and and_14 (and_14_out, nand_1_out, nand_4_out, A1, B1);
  and and_15 (and_15_out, not_8_out, not_9_out, nand_3_out, nand_2_out);
  and and_16 (and_16_out, nand_1_out, nand_3_out, nand_4_out, A2, not_9_out);
  and and_17 (and_17_out, nand_2_out, nand_4_out, not_8_out, B2);
  and and_18 (and_18_out, not_8_out, not_9_out, nand_1_out, nand_4_out, nor_9_out);
  and and_19 (and_19_out, nand_2_out, nand_3_out, A2, not_9_out);
  and and_20 (and_20_out, nand_2_out, nand_3_out, not_8_out, B2);
  and and_21 (and_21_out, nand_1_out, nand_4_out, A2, B2);
  and and_22 (and_22_out, not_10_out, not_11_out, nand_3_out, nand_2_out);
  and and_23 (and_23_out, nand_1_out, nand_3_out, nand_4_out, A3, not_11_out);
  and and_24 (and_24_out, nand_2_out, nand_4_out, not_10_out, B3);
  and and_25 (and_25_out, not_10_out, not_11_out, nand_1_out, nand_4_out, nor_9_out);
  and and_26 (and_26_out, nand_2_out, nand_3_out, A3, not_11_out);
  and and_27 (and_27_out, nand_2_out, nand_3_out, not_10_out, B3);
  and and_28 (and_28_out, nand_1_out, nand_4_out, A3, B3);
  and and_29 (and_29_out, not_1_out, not_2_out);
  and and_30 (and_30_out, not_2_out, not_14_out);
  nand nand_3 (nand_3_out, not_1_out, not_13_out);
  nand nand_4 (nand_4_out, not_12_out, not_13_out, not_3_out);
  nor nor_1 (nor_1_out, and_1_out, and_2_out, and_3_out);
  nor nor_2 (nor_2_out, and_4_out, and_5_out, and_6_out, and_7_out);
  nor nor_3 (nor_3_out, and_8_out, and_9_out, and_10_out);
  nor nor_4 (nor_4_out, and_11_out, and_12_out, and_13_out, and_14_out);
  nor nor_5 (nor_5_out, and_15_out, and_16_out, and_17_out);
  nor nor_6 (nor_6_out, and_18_out, and_19_out, and_20_out, and_21_out);
  nor nor_7 (nor_7_out, and_22_out, and_23_out, and_24_out);
  nor nor_8 (nor_8_out, and_25_out, and_26_out, and_27_out, and_28_out);
  and and_31 (and_31_out, not_1_out, not_14_out);
  nor nor_9 (nor_9_out, and_31_out, and_30_out);
  nor nor_10 (nor_10_out, and_29_out, not_14_out);
  nand nand_5 (nand_5_out, Cn, nor_10_out);
  and and_32 (and_32_out, Cn, nor_1_out, nor_10_out);
  and and_33 (and_33_out, nor_1_out, nor_2_out, nor_10_out);
  and and_34 (and_34_out, Cn, nor_1_out, nor_3_out, nor_10_out);
  and and_35 (and_35_out, nor_1_out, nor_3_out, nor_2_out, nor_10_out);
  and and_36 (and_36_out, nor_5_out, nor_4_out, nor_10_out);
  and and_37 (and_37_out, Cn, nor_1_out, nor_3_out, nor_5_out, nor_10_out);
  and and_38 (and_38_out, nor_1_out, nor_3_out, nor_5_out, nor_2_out, nor_10_out);
  and and_39 (and_39_out, nor_3_out, nor_5_out, nor_4_out, nor_10_out);
  and and_40 (and_40_out, nor_5_out, nor_6_out, nor_10_out);
  and and_41 (and_41_out, nor_1_out, nor_3_out, nor_5_out, nor_7_out, nor_2_out);
  and and_42 (and_42_out, nor_3_out, nor_5_out, nor_7_out, nor_4_out);
  and and_43 (and_43_out, nor_5_out, nor_7_out, nor_6_out);
  and and_44 (and_44_out, nor_7_out, nor_8_out);
  nand nand_6 (nand_6_out, Cn, nor_1_out, nor_3_out, nor_5_out, nor_7_out);
  nor nor_11 (nor_11_out, and_32_out, and_33_out);
  nor nor_12 (nor_12_out, and_34_out, and_35_out, and_36_out);
  nor nor_13 (nor_13_out, and_37_out, and_38_out, and_39_out, and_40_out);
  nor nor_14 (nor_14_out, and_41_out, and_42_out, and_43_out, and_44_out);
  and and_45 (and_45_out, nor_14_out, nand_6_out);
  nand nand_7 (Cn4, nor_14_out, nand_6_out);
  xor xor_1 (F0, nand_5_out, nor_2_out);
  xor xor_2 (F1, nor_11_out, nor_4_out);
  xor xor_3 (F2, nor_12_out, nor_6_out);
  xor xor_4 (F3, nor_13_out, nor_8_out);
  xor xor_5 (OVR, nor_13_out, and_45_out);
endmodule

module REVERSE16 (
  input  [15:0] MY_IN,
  output [15:0] MY_OUT
);


  assign MY_OUT = {MY_IN[0], MY_IN[1], MY_IN[2], MY_IN[3], MY_IN[4], MY_IN[5], MY_IN[6], MY_IN[7], MY_IN[8], MY_IN[9], MY_IN[10], MY_IN[11], MY_IN[12], MY_IN[13], MY_IN[14], MY_IN[15]};
endmodule

module REVERSE8 (
  input  [7:0] MY_IN,
  output [7:0] MY_OUT
);


  assign MY_OUT = {MY_IN[0], MY_IN[1], MY_IN[2], MY_IN[3], MY_IN[4], MY_IN[5], MY_IN[6], MY_IN[7]};
endmodule
