// Logisim project Microcode.circ as structural Verilog: 1 circuit, main circuit Microcode
module Microcode (
  input  CLK_M,
  input  nFP_WRITE,
  input  nRESET,
  input  nDMA_ACQ,
  input  [3:0] ENCODER,
  input  [7:0] DBUS,
  input  INIT_INST,
  input  MSWC,
  input  MSWZ,
  input  FAULT_PENDING,
  input  MSWS,
  input  nDO_BRANCH,
  input  MSWV,
  output [3:0] LATCH,
  output XL_MAR,
  output R_RW,
  output XL_MDR_LO,
  output XL_MDR_HI,
  output nE_MDR_LO,
  output PRIV,
  output XL_MODE,
  output nE_MDR_HI,
  output XL_PAGING,
  output [3:0] MISC,
  output [3:0] EL,
  output [1:0] ER,
  output [1:0] RIMM_VAL,
  output [7:0] IR,
  output ALUOP_SZ,
  output [1:0] ALU_OP,
  output USE_CARRY,
  output LATCH_SZ,
  output RUSER_PTB,
  output CODE_PTB,
  output nNEXT0
);

  wire NEGATE_BR, not_1_out, U11_y, U12A_out, U12B_out, U13A_out, U13B_out, U13C_out, U14A_out, U14D_out,
       U14E_out, U21_out, U24_out, U61B_out;
  wire [7:0] NEXT_INST;
  wire [8:0] U61D_out;
  wire [16:15] register_1_q;
  wire [39:0] rom_1_data;

  not U14E (U14E_out, MSWC);
  xor U12B (U12B_out, MSWS, MSWV);
  IC_74273 ic_74273_1 (
    .Y2(IR[1]), .Y3(IR[2]), .Y1(IR[0]), .Y4(IR[3]), .Y5(IR[4]), .Y6(IR[5]), .Y7(IR[6]), .Y8(IR[7]),
    .D2(DBUS[1]), .D3(DBUS[2]), .D1(DBUS[0]), .D4(DBUS[3]), .D5(DBUS[4]), .D6(DBUS[5]), .D7(DBUS[6]),
    .D8(DBUS[7]), .CLK(INIT_INST), .CLR(1'b1));
  or U13C (U13C_out, U14E_out, MSWZ);
  or U13B (U13B_out, U12B_out, MSWZ);
  not U14A (U14A_out, MSWZ);
  IC_74151 U11 (
    .Y(U11_y), .C(U12B_out), .D(U13B_out), .E(U14E_out), .A(MSWZ), .F(U13C_out), .G(MSWZ), .J(U14A_out),
    .S0(IR[3]), .S1(IR[2]), .S2(IR[1]), .OE(1'b0), .B(MSWZ));  // open: Z
  nand U24 (U24_out, NEXT_INST[0], NEXT_INST[1], NEXT_INST[2], NEXT_INST[3], NEXT_INST[4], NEXT_INST[5], NEXT_INST[6], NEXT_INST[7]);
  xor U12A (U12A_out, NEGATE_BR, U11_y);
  Multiplexer #(.enable("false"), .select(2), .width(8)) multiplexer_1 (
    .in0({4'b0000, ENCODER[0], ENCODER[1], ENCODER[2], ENCODER[3]}),
    .in1({IR[0], IR[1], IR[2], IR[3], IR[4], IR[5], IR[6], IR[7]}),
    .in2({4'b0000, ENCODER[0], ENCODER[1], ENCODER[2], ENCODER[3]}),
    .in3({NEXT_INST[0], NEXT_INST[1], NEXT_INST[2], NEXT_INST[3], NEXT_INST[4], NEXT_INST[5], NEXT_INST[6], NEXT_INST[7]}),
    .out(U61D_out[7:0]), .sel({U61D_out[8], nNEXT0}));
  or U61D (U61D_out[8], U24_out, FAULT_PENDING);
  not U14D (U14D_out, FAULT_PENDING);
  or U13A (U13A_out, nDO_BRANCH, U12A_out);
  or U21 (U21_out, NEXT_INST[0], NEXT_INST[1], NEXT_INST[2], NEXT_INST[3], NEXT_INST[4], NEXT_INST[5], NEXT_INST[6], NEXT_INST[7]);
  and U44B (nNEXT0, U14D_out, U13A_out, U21_out);
  ROM #(.addrWidth(9), .dataWidth(40)) rom_1 (.addr(U61D_out), .data(rom_1_data));
  Register #(.width(40)) register_1 (
    .D(rom_1_data), .en(1'b1), .clk(CLK_M),
    .Q({CODE_PTB, RUSER_PTB, NEGATE_BR, LATCH_SZ, USE_CARRY, ALU_OP[0], ALU_OP[1], ALUOP_SZ, RIMM_VAL[0], RIMM_VAL[1], ER[0], ER[1], EL[0], EL[1], EL[2], EL[3], MISC[0], MISC[1], MISC[2], MISC[3], XL_PAGING, XL_MODE, PRIV, register_1_q, XL_MDR_HI, XL_MDR_LO, XL_MAR, LATCH[0], LATCH[1], LATCH[2], LATCH[3], NEXT_INST[0], NEXT_INST[1], NEXT_INST[2], NEXT_INST[3], NEXT_INST[4], NEXT_INST[5], NEXT_INST[6], NEXT_INST[7]}),
    .clr(not_1_out));
  not not_1 (not_1_out, nRESET);
  not U14C (nE_MDR_LO, register_1_q[15]);
  or U61B (U61B_out, nFP_WRITE, nDMA_ACQ);
  not U14B (nE_MDR_HI, register_1_q[16]);
  nand U25A (R_RW, U61B_out, nE_MDR_HI, nE_MDR_LO);

  // Notes on the sheet:
  //   contents of rom_1 (hex, n*v repeats v):
  //   96d3201300 9653005316 9653005338 9653005374 96530053c8 96530053a4 96530053c8 82d70010dd 965300537c
  //   96530053a4 96530053c8 96530053b2 96530053c8 96530053a4 965300535a 96530053a4 9653005374 12d1000600
  //   9653005384 12d6020900 9653005318 9653005354 9653005318 4126000ee 96530053a2 9653005354 9653005318
  //   965300538a 9653005318 9653005354 965300337a 9653005354 12d400086c 96530073e6 96530033d8 12d70008bd
  //   9653003348 9653003324 9653003348 965300538e 9653005382 9653003324 9653003348 965300532a 9653003348
  //   9653003324 965300533a 9653003324 2d500109c 96530033f4 9653005383 6d6001017 96530053fd 9653005303
  //   96530053fd 42d702103d 9653005392 9653005303 96530053fd 96530053ea 96530053fd 9653005303 9653005306
  //   9653005303 12d200086c 12d30008d6 12d7000200 12d600087d 12d100086c 12d7000873 12d70008cb 96530073a6
  //   965300537c 12d6000700 13d6000600 96530053b2 92d6001300 13d7000700 965300535a 12d2000600 2d500109c
  //   20045 12d600080b 200ab 6d600104f 12d70008b3 12d60008f3 412620081 96530053a2 12d7000600 12d600088b
  //   965300538a 965300339d 6d600104f 9653007386 30007f 12d600086c 96530033db 12d60008e8 12d7800700
  //   12d500086c 96530053b4 0 12d60008c3 9653005382 12d6000200 96530053b4 965300532a 12d6000848 12d6000400
  //   965300533a 12d5000600 2d500109c 965300534c 406600000 9653005326 c2d702100e 9653005374 2d700106b
  //   12d6000813 9653005392 12d8000894 9653005374 96530053ea 12d60008e8 9653005374 12d600089a 12d8000894
  //   965300537c 9653003342 9653005338 96530053b2 96530053c8 96530053a4 96530053c8 12d4000600 965300333c
  //   96530053a4 96530053c8 9653003352 96530053c8 96530053a4 965300535a 96530053a4 2d500109c 96530053b4
  //   9653005384 965300538a 9653005318 9653005354 9653005318 41262005e 96530053a2 9653005354 9653005318
  //   9653003372 9653005318 9653005354 96530033fa 9653005354 9653005382 9653003362 506600000 965300532a
  //   6d6001017 12d8000824 6d6001017 6d800088e 96530033fc 12d8000824 6d6001017 965300334a 6d6001017
  //   96530053b4 965300533a 12d8000824 2d500109c 965300338c 9653007304 96530053ea 96530073e8 9653007394
  //   96530073e8 12d700081a 9653005392 9653007394 96530073e8 96530033aa 96530073e8 9653007394 9653005346
  //   9653007394 12db00086c 9653005366 9653005338 12d6800600 96530053c8 96530053a4 96530053c8 49700103b
  //   965300537c 96530053a4 96530053c8 96530053b2 96530053c8 96530053a4 965300535a 96530053a4 2d500109c
  //   400000 9653005384 12d6000500 9653005318 9653005354 9653005318 2d7001076 96530053a2 9653005354
  //   9653005318 965300538a 9653005318 9653005354 96530073c6 9653005354 12d700086c 96530033db 12d70008d8
  //   12d70008e8 12d7000848 12d7000824 12d7000848 12d70008c3 9653005382 12d7000824 12d7000848 965300532a
  //   12d7000848 12d7000824 965300533a 12d7000824 2d500109c 965300532c 12d7000804 96530053b4 12d70008e8
  //   12d7000894 12d70008e8 12d7000813 9653005392 12d7000894 12d70008e8 96530053ea 12d70008e8 12d7000894
  //   12d700089a 12d7000894 96507033cc 96d3001300 82d30030fa 9653003394 406600000 1218000400 9653003386
  //   2d6003000 60f001000 12d6000800 650011032 1607000700 b653b07334 650003000 6500043 6d6001000 2d0d000a1
  //   6d0009000 82d30030c6 412600000 82d3003000 12d8000200 9653003300 2000 9653003328 6d0011000 1c06600600
  //   82d3001000 82d3011000 12db000543 2d7001000 12d0004700 2d0d000a1 165000867e 82d3003086 2000b00000
  //   5066000d4 650003000 96530033a6 650011000 60f001000 6d0009000 965300334a 1606000700 9653003300
  //   2d8d00000 6d0001000 4000 12d00003a1 6d0011000 82d3009000 12d8800ffe 9603001300 650005000 16d0009500
  //   6d7001000 9653003398 12d3000600 96530033ba 650005000 60f001000 6500043 2d6003000 0 2d0d000a1
  //   2d7001000 60f001000 82d3001000 60f001000 2d5001000 96530033c6 650009000 106600600 6d0011000
  //   60f001000 1607000600 9653003300 650005000 605001000 2000 12d00003a1 12d5000800 60f001000 418600000
  //   9653003364 650003000 140300086c 4000 82d3003000 16d0009500 96530033da 3657b00701 1650003500 10007f
  //   2000b20000 0 2d0d000a1 218a40000 60f001000 2000b00000 60f001000 650005000 96530033e6 1497000700
  //   82d3003000 12d2000800 12d700080a 2d6003000 6d5001000 1650002500 12d0010543 6d7001000 12d00003a1
  //   6d0009000 60f001000 1606000600 b653b03334 12d8000600 2000 12d0004700 650005000 650005000 2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
endmodule
