// Logisim project REGS.circ as structural Verilog: 1 circuit, main circuit REGS
module REGS (
  input  [15:0] Z,
  input  [12:0] L_CTLBUS,
  input  COMMIT,
  input  [14:0] nEL_CTLBUS,
  input  nDMA_ACK,
  input  nRW,
  input  [5:0] xBUS,
  input  nRESET,
  input  [1:0] IMMVAL,
  output L_FPL,
  output [15:0] L,
  output nHALT,
  output [7:0] D,
  output [7:0] DBUS,
  output [15:0] R,
  output [15:0] T,
  output [15:0] MAR
);

  GREGS gregs_1 (
    .L(L), .Z(Z), .L_SP(nEL_CTLBUS[4]), .nEL_SSP(L_CTLBUS[8]), .L_SSP(L_CTLBUS[10]), .nEL_PC(L_CTLBUS[3]),
    .L_PC(nEL_CTLBUS[11]), .L_A_HI(L_CTLBUS[1]), .nEL_TPC(nEL_CTLBUS[5]), .COMMIT(COMMIT),
    .n_EL_A(L_CTLBUS[7]), .L_A_LO(L_CTLBUS[4]), .L_B_HI(nEL_CTLBUS[10]), .n_EL_B(nEL_CTLBUS[8]),
    .L_B_LO(nEL_CTLBUS[7]), .nEL_C(nEL_CTLBUS[3]), .L_C(L_CTLBUS[2]), .nEL_DP(nEL_CTLBUS[6]),
    .L_DP(L_CTLBUS[11]), .nEL_SP(L_CTLBUS[5]));
  MDR mdr_1 (
    .XL_MDR_HI(xBUS[5]), .XL_MDR_LO(xBUS[4]), .Z(Z), .nDMA_ACK(nDMA_ACK), .nRW(nRW),
    .nE_MDR_HI(nEL_CTLBUS[14]), .L_MDR_HI(L_CTLBUS[9]), .nEL_MDR(nEL_CTLBUS[2]), .nER_MDR(nEL_CTLBUS[9]),
    .L_MDR_LO(L_CTLBUS[6]), .COMMIT(COMMIT), .nE_MDR_LO(nEL_CTLBUS[13]), .D(D), .DBUS(DBUS), .L(L), .R(R),
    .T(T));
  SREGS sregs_1 (
    .L_MAR(L_CTLBUS[12]), .Z(Z), .nRESET(nRESET), .nEL_MAR(nEL_CTLBUS[1]), .IMMVAL(IMMVAL),
    .nER_IMM(nEL_CTLBUS[12]), .MAR(MAR), .L(L), .R(R));

  assign L_FPL = L_CTLBUS[0];
  assign nHALT = nEL_CTLBUS[0];
endmodule
