// Logisim project SRAM.circ as structural Verilog: 1 circuit, main circuit SRAM
module SRAM (
  input  [21:0] A,
  input  MEMORY,
  input  nWR,
  input  nRD,
  output [7:0] DBUS
);

  wire and_1_out, and_2_out, not_1_out, not_2_out;

  not not_1 (not_1_out, nWR);
  not not_2 (not_2_out, nRD);
  and and_1 (and_1_out, MEMORY, not_1_out);
  and and_2 (and_2_out, MEMORY, not_2_out);
  RAM #(.addrWidth(22), .trigger("low")) ram_1 (.addr(A), .we(and_1_out), .oe(and_2_out), .din(DBUS), .dout(DBUS));
endmodule
