// Logisim project SREGS.circ as structural Verilog: 1 circuit, main circuit SREGS
module SREGS (
  input  L_MAR,
  input  [15:0] Z,
  input  nRESET,
  input  nEL_MAR,
  input  [1:0] IMMVAL,
  input  nER_IMM,
  output [15:0] MAR,
  output [15:0] L,
  output [15:0] R
);

  IC_74273 ic_74273_1 (
    .Y2(MAR[1]), .Y3(MAR[2]), .Y1(MAR[0]), .Y4(MAR[3]), .Y5(MAR[4]), .Y6(MAR[5]), .Y7(MAR[6]), .Y8(MAR[7]),
    .D2(Z[1]), .D3(Z[2]), .D1(Z[0]), .D4(Z[3]), .D5(Z[4]), .D6(Z[5]), .D7(Z[6]), .D8(Z[7]), .CLK(L_MAR),
    .CLR(nRESET));
  IC_74273 ic_74273_2 (
    .Y2(MAR[9]), .Y3(MAR[10]), .Y1(MAR[8]), .Y4(MAR[11]), .Y5(MAR[12]), .Y6(MAR[13]), .Y7(MAR[14]),
    .Y8(MAR[15]), .D2(Z[9]), .D3(Z[10]), .D1(Z[8]), .D4(Z[11]), .D5(Z[12]), .D6(Z[13]), .D7(Z[14]),
    .D8(Z[15]), .CLK(L_MAR), .CLR(nRESET));
  IC_74244 ic_74244_1 (
    .Y3(L[2]), .Y4(L[3]), .Z1(L[4]), .Y1(L[0]), .Z2(L[5]), .Z3(L[6]), .Z4(L[7]), .Y2(L[1]), .A3(MAR[2]),
    .A4(MAR[3]), .OEA(nEL_MAR), .B1(MAR[4]), .A1(MAR[0]), .B2(MAR[5]), .B3(MAR[6]), .B4(MAR[7]),
    .OEB(nEL_MAR), .A2(MAR[1]));
  IC_74244 ic_74244_2 (
    .Y3(L[10]), .Y4(L[11]), .Z1(L[12]), .Y1(L[8]), .Z2(L[13]), .Z3(L[14]), .Z4(L[15]), .Y2(L[9]),
    .A3(MAR[10]), .A4(MAR[11]), .OEA(nEL_MAR), .B1(MAR[12]), .A1(MAR[8]), .B2(MAR[13]), .B3(MAR[14]),
    .B4(MAR[15]), .OEB(nEL_MAR), .A2(MAR[9]));
  IC_74244 ic_74244_3 (
    .Y3(R[2]), .Y4(R[3]), .Z1(R[4]), .Y1(R[0]), .Z2(R[5]), .Z3(R[6]), .Z4(R[7]), .Y2(R[1]), .A3(IMMVAL[0]),
    .A4(IMMVAL[0]), .OEA(nER_IMM), .B1(IMMVAL[0]), .A1(IMMVAL[0]), .B2(IMMVAL[0]), .B3(IMMVAL[0]),
    .B4(IMMVAL[0]), .OEB(nER_IMM), .A2(IMMVAL[0]));
  IC_74244 ic_74244_4 (
    .Y3(R[10]), .Y4(R[11]), .Z1(R[12]), .Y1(R[8]), .Z2(R[13]), .Z3(R[14]), .Z4(R[15]), .Y2(R[9]),
    .A3(IMMVAL[0]), .A4(IMMVAL[0]), .OEA(nER_IMM), .B1(IMMVAL[0]), .A1(IMMVAL[0]), .B2(IMMVAL[0]),
    .B3(IMMVAL[0]), .B4(IMMVAL[1]), .OEB(nER_IMM), .A2(IMMVAL[0]));
endmodule
